// Logisim project AnotherCpu.circ as structural Verilog: 9 circuits, main circuit main
module main (
  input  in_1,
  input  [15:0] Color,
  input  in_3,
  input  in_4
);

  wire ADD, ALU, alu_1_equal, alu_1_greater_than, alu_1_less_than, and_1_out, and_2_out, and_3_out,
       and_5_out, and_7_out, and_8_out, and_9_out, Clk, clock_1_out, CMP, controlled_buffer_2_out, CPR, DWP,
       EQ, GT, HLT, IRCO, JGT, JIE, JLT, JMP, lcd_video_1_p8, lcd_video_1_p9, LDM, LDR, LT, MCL, NAND, NOPC,
       not_1_out, not_2_out, not_3_out, not_4_out, not_5_out, not_6_out, not_7_out, not_8_out, not_9_out,
       not_10_out, not_11_out, not_13_out, not_14_out, not_15_out, not_16_out, not_17_out, not_18_out,
       not_19_out, not_20_out, not_21_out, not_22_out, not_23_out, not_24_out, not_25_out, not_26_out,
       not_28_out, not_29_out, not_30_out, or_1_out, or_2_out, or_3_out, or_4_out, or_6_out, or_8_out,
       or_9_out, or_10_out, R, RCL, REset_screen_out, ResIRClock, s_r_ff_4_q, s_r_ff_5_q, s_r_ff_6_q,
       s_r_ff_7_q, SRV, SUB, SyncIR, undriven, undriven_2, undriven_3, undriven_4, undriven_5;
  wire [3:0] RAA, RBA, RFA;
  wire [6:0] not_27_out;
  wire [11:0] controlled_buffer_1_out, controlled_buffer_3_out, counter_1_q, MA, MEM;
  wire [15:0] alu_1_output, controlled_buffer_11_out, controlled_buffer_12_out, RAD, RBD, RFI;
  wire [15:7] not_27_out_2;
  wire [25:0] bit_extender_1_out, MDT, ram_1_data;
  wire [25:20] Instruction_Register_q;
  wire [31:0] xytomatrix32_1_out_6, xytomatrix32_1_out_7, xytomatrix32_1_out_8, xytomatrix32_1_out_9,
       xytomatrix32_1_out_10, xytomatrix32_1_out_11, xytomatrix32_1_out_12, xytomatrix32_1_out_13,
       xytomatrix32_1_out_14, xytomatrix32_1_out_15, xytomatrix32_1_out_16, xytomatrix32_1_out_17,
       xytomatrix32_1_out_18, xytomatrix32_1_out_19, xytomatrix32_1_out_20, xytomatrix32_1_out_21,
       xytomatrix32_1_out_22, xytomatrix32_1_out_23, xytomatrix32_1_out_24, xytomatrix32_1_out_25,
       xytomatrix32_1_out_26, xytomatrix32_1_out_27, xytomatrix32_1_out_28, xytomatrix32_1_out_29,
       xytomatrix32_1_out_30, xytomatrix32_1_out_31, xytomatrix32_1_out_32, xytomatrix32_1_out_33,
       xytomatrix32_1_out_34, xytomatrix32_1_out_35, xytomatrix32_1_out_36, xytomatrix32_1_out_37;

  Clock clock_1 (.out(clock_1_out));
  Button Reboot (.out(R));
  Button Sync_IR (.out(SyncIR));
  assign controlled_buffer_1_out = or_1_out ? MEM : 12'bz;  // Controlled_Buffer controlled_buffer_1
  or or_1 (or_1_out, JMP, and_1_out, and_3_out, and_2_out);
  Pull_Resistor pull_resistor_1 (.node(controlled_buffer_1_out));
  not not_1 (not_1_out, or_1_out);
  assign controlled_buffer_2_out = not_2_out ? Clk : 1'bz;  // Controlled_Buffer controlled_buffer_2
  not not_2 (not_2_out, or_2_out);
  or or_2 (or_2_out, MCL, LDM, LDR);
  Decoder6Bit decoder6bit_1 (
    .Select(Instruction_Register_q), .out_2(NOPC), .out_3(ADD), .out_4(SUB), .out_7(CMP), .out_8(NAND),
    .out_14(JMP), .out_15(HLT), .out_16(SRV), .out_17(CPR), .out_18(RCL), .out_19(MCL), .out_20(LDM),
    .out_21(LDR), .out_22(JIE), .out_23(JLT), .out_24(JGT), .out_25(DWP));  // open: out_5, out_6, out_9, out_10, out_11, out_12, out_13, out_26, out_27, out_28, out_29, out_30, out_31, out_32, out_33, out_34, out_35, out_36, out_37, out_38, out_39, out_40, out_41, out_42, out_43, out_44, out_45, out_46, out_47, out_48, out_49, out_50, out_51, out_52, out_53, out_54, out_55, out_56, out_57, out_58, out_59, out_60, out_61, out_62, out_63, out_64, out_65
  Transistor transistor_1 (.in(clock_1_out), .out(Clk), .gate(HLT));
  and and_1 (and_1_out, JGT, GT);
  Counter #(.width(12), .max('hfff)) counter_1 (
    .load(or_1_out), .D(controlled_buffer_1_out), .count(not_1_out), .Q(counter_1_q),
    .clk(controlled_buffer_2_out), .clr(R));  // open: carry
  and and_2 (and_2_out, JLT, LT);
  not not_3 (not_3_out, or_2_out);
  assign controlled_buffer_3_out = not_3_out ? counter_1_q : 12'bz;  // Controlled_Buffer controlled_buffer_3
  assign controlled_buffer_3_out = or_2_out ? MA : 12'bz;  // Controlled_Buffer controlled_buffer_4
  or or_3 (or_3_out, MCL, LDR);
  assign MDT = MCL ? {26{1'b0}} : 26'bz;  // Controlled_Buffer controlled_buffer_5
  or or_4 (or_4_out, MCL, LDM, LDR);
  Transistor #(.\type ("n"), .width(12)) transistor_2 (.in(MEM), .out(MA), .gate(or_4_out));
  Pull_Resistor pull_resistor_2 (.node(MA));
  Pull_Resistor pull_resistor_3 (.node(MEM));
  assign bit_extender_1_out = {{10{1'b0}}, RAD};  // Bit_Extender bit_extender_1
  and and_3 (and_3_out, JIE, EQ);
  and and_4 (ResIRClock, ~ram_1_data[20], ~ram_1_data[21], ~ram_1_data[22], ~ram_1_data[23], ~ram_1_data[24], ~ram_1_data[25]);  // AND_Gate
  not not_4 (not_4_out, not_5_out);
  not not_5 (not_5_out, not_6_out);
  not not_6 (not_6_out, not_7_out);
  not not_7 (not_7_out, not_8_out);
  not not_8 (not_8_out, not_9_out);
  not not_9 (not_9_out, not_10_out);
  not not_10 (not_10_out, not_11_out);
  not not_11 (not_11_out, Clk);
  assign MDT = LDR ? bit_extender_1_out : 26'bz;  // Controlled_Buffer controlled_buffer_6
  and and_5 (and_5_out, ~MCL, ~LDM, ~LDR);  // AND_Gate
  or or_5 (IRCO, and_5_out, ResIRClock);
  RAM #(.addrWidth(12), .dataWidth(26), .bus("separate")) ram_1 (
    .addr(controlled_buffer_3_out), .din(MDT), .data(ram_1_data), .str(or_3_out), .clk(Clk));  // open: sel, ld, clr
  Pull_Resistor pull_resistor_4 (.node(ram_1_data));
  or or_6 (or_6_out, SyncIR, Clk);
  // AND_Gate and_6 has open pins: in1=Clk, out=open
  // NOT_Gate not_12 has open pins: in=not_13_out, out=open
  not not_13 (not_13_out, not_14_out);
  not not_14 (not_14_out, not_15_out);
  not not_15 (not_15_out, not_16_out);
  not not_16 (not_16_out, not_17_out);
  not not_17 (not_17_out, not_18_out);
  not not_18 (not_18_out, not_19_out);
  not not_19 (not_19_out, not_20_out);
  not not_20 (not_20_out, not_4_out);
  assign RFI = RCL ? {16{1'b0}} : 16'bz;  // Controlled_Buffer controlled_buffer_7
  assign RFA = RCL ? RAA : 4'bz;  // Controlled_Buffer controlled_buffer_8
  // OR_Gate or_7 has open pins: in0=MCL, in1=LDM, in2=LDR, in3=ResIRClock, out=open
  assign RFI = LDM ? ram_1_data[15:0] : 16'bz;  // Controlled_Buffer controlled_buffer_9
  Register #(.width(26), .trigger("falling")) Instruction_Register (
    .D(ram_1_data), .en(IRCO), .Q({Instruction_Register_q, RAA, RBA, MEM}), .clk(or_6_out), .clr(or_8_out));
  buf or_8 (or_8_out, R);  // OR_Gate
  or or_9 (or_9_out, ALU, SRV, LDM);
  assign RFA = or_9_out ? RAA : 4'bz;  // Controlled_Buffer controlled_buffer_10
  or or_10 (or_10_out, LDM, ADD, SUB, CPR, SRV, RCL, NAND);
  or or_11 (ALU, ADD, NAND, SUB, CMP);
  RegisterBank registerbank_1 (
    .Select(RFA), .Input_Data(RFI), .Clock(Clk), .A_Select(RAA), .B_Select(RBA), .A_Output(RAD),
    .B_Output(RBD), .Write(or_10_out));  // open: Master_Reset
  assign controlled_buffer_11_out = ALU ? RAD : 16'bz;  // Controlled_Buffer controlled_buffer_11
  assign controlled_buffer_12_out = ALU ? RBD : 16'bz;  // Controlled_Buffer controlled_buffer_12
  ALU alu_1 (
    .A(controlled_buffer_11_out), .Op_Code(Instruction_Register_q[23:20]), .Output(alu_1_output),
    .Greater_Than(alu_1_greater_than), .Equal(alu_1_equal), .Less_Than(alu_1_less_than),
    .B(controlled_buffer_12_out));  // open: Carry_Borrow, Negative, Zero, C_Out, B_Out, A_2, B_2, B_3, Overflow
  assign RFI = ALU ? alu_1_output : 16'bz;  // Controlled_Buffer controlled_buffer_13
  assign RFI = SRV ? {RBA, MEM} : 16'bz;  // Controlled_Buffer controlled_buffer_14
  assign RFA = CPR ? RAA : 4'bz;  // Controlled_Buffer controlled_buffer_15
  assign RFI = CPR ? RBD : 16'bz;  // Controlled_Buffer controlled_buffer_16
  not not_21 (not_21_out, CMP);
  and and_7 (and_7_out, CMP, not_22_out);
  not not_22 (not_22_out, not_23_out);
  not not_23 (not_23_out, not_21_out);
  and and_8 (and_8_out, CMP, Clk);
  and and_9 (and_9_out, in_4, not_24_out);
  not not_24 (not_24_out, not_25_out);
  not not_25 (not_25_out, not_26_out);
  not not_26 (not_26_out, in_4);
  S_R_Flip_Flop #(.trigger("falling")) s_r_ff_1 (
    .S(alu_1_greater_than), .clk(and_8_out), .R(1'b0), .Q(GT), .reset(and_7_out));  // open: Qn, preset, en
  S_R_Flip_Flop #(.trigger("falling")) s_r_ff_2 (
    .S(alu_1_equal), .clk(and_8_out), .R(1'b0), .Q(EQ), .reset(and_7_out));  // open: Qn, preset, en
  S_R_Flip_Flop #(.trigger("falling")) s_r_ff_3 (
    .S(alu_1_less_than), .clk(and_8_out), .R(1'b0), .Q(LT), .reset(and_7_out));  // open: Qn, preset, en
  S_R_Flip_Flop s_r_ff_4 (.S(in_3), .clk(in_3), .Q(s_r_ff_4_q), .reset(and_9_out));  // open: R, Qn, preset, en
  Button REset_screen (.out(REset_screen_out));
  // OR_Gate or_12 has open pins: in0=Clk, in1=SyncIR, out=open
  // Probe on DWP
  // Probe on RAD[6:0]
  // Probe on not_27_out
  assign {not_27_out_2, not_27_out} = ~RBD;  // NOT_Gate not_27, 16 bits wide
  not not_28 (not_28_out, undriven);
  not not_29 (not_29_out, not_28_out);
  not not_30 (not_30_out, not_29_out);
  // AND_Gate and_10 has open pins: in0=undriven, in1=not_30_out, out=open
  DotMatrix #(.matrixcols(32), .matrixrows(32)) dotmatrix_1 (
    .col0(xytomatrix32_1_out_6), .col1(xytomatrix32_1_out_7), .col2(xytomatrix32_1_out_8),
    .col3(xytomatrix32_1_out_9), .col4(xytomatrix32_1_out_10), .col5(xytomatrix32_1_out_11),
    .col6(xytomatrix32_1_out_12), .col7(xytomatrix32_1_out_13), .col8(xytomatrix32_1_out_14),
    .col9(xytomatrix32_1_out_15), .col10(xytomatrix32_1_out_16), .col11(xytomatrix32_1_out_17),
    .col12(xytomatrix32_1_out_18), .col13(xytomatrix32_1_out_19), .col14(xytomatrix32_1_out_20),
    .col15(xytomatrix32_1_out_21), .col16(xytomatrix32_1_out_22), .col17(xytomatrix32_1_out_23),
    .col18(xytomatrix32_1_out_24), .col19(xytomatrix32_1_out_25), .col20(xytomatrix32_1_out_26),
    .col21(xytomatrix32_1_out_27), .col22(xytomatrix32_1_out_28), .col23(xytomatrix32_1_out_29),
    .col24(xytomatrix32_1_out_30), .col25(xytomatrix32_1_out_31), .col26(xytomatrix32_1_out_32),
    .col27(xytomatrix32_1_out_33), .col28(xytomatrix32_1_out_34), .col29(xytomatrix32_1_out_35),
    .col30(xytomatrix32_1_out_36), .col31(xytomatrix32_1_out_37));
  // LCD_Video lcd_video_1: pin names not known; wires that end beside it: R, Clk, DWP, CMP, RAD[6:0], not_27_out, Color, lcd_video_1_p8, lcd_video_1_p9
  XYToMatrix32 xytomatrix32_1 (
    .X(RAD[4:0]), .Y(RBD[4:0]), .write(DWP), .clear(R), .clock(Clk), .out_6(xytomatrix32_1_out_6),
    .out_7(xytomatrix32_1_out_7), .out_8(xytomatrix32_1_out_8), .out_9(xytomatrix32_1_out_9),
    .out_10(xytomatrix32_1_out_10), .out_11(xytomatrix32_1_out_11), .out_12(xytomatrix32_1_out_12),
    .out_13(xytomatrix32_1_out_13), .out_14(xytomatrix32_1_out_14), .out_15(xytomatrix32_1_out_15),
    .out_16(xytomatrix32_1_out_16), .out_17(xytomatrix32_1_out_17), .out_18(xytomatrix32_1_out_18),
    .out_19(xytomatrix32_1_out_19), .out_20(xytomatrix32_1_out_20), .out_21(xytomatrix32_1_out_21),
    .out_22(xytomatrix32_1_out_22), .out_23(xytomatrix32_1_out_23), .out_24(xytomatrix32_1_out_24),
    .out_25(xytomatrix32_1_out_25), .out_26(xytomatrix32_1_out_26), .out_27(xytomatrix32_1_out_27),
    .out_28(xytomatrix32_1_out_28), .out_29(xytomatrix32_1_out_29), .out_30(xytomatrix32_1_out_30),
    .out_31(xytomatrix32_1_out_31), .out_32(xytomatrix32_1_out_32), .out_33(xytomatrix32_1_out_33),
    .out_34(xytomatrix32_1_out_34), .out_35(xytomatrix32_1_out_35), .out_36(xytomatrix32_1_out_36),
    .out_37(xytomatrix32_1_out_37));
  S_R_Flip_Flop #(.trigger("falling")) s_r_ff_5 (
    .clk(undriven_5), .R(undriven_4), .Q(s_r_ff_5_q), .reset(lcd_video_1_p8));  // open: S, Qn, preset, en
  S_R_Flip_Flop #(.trigger("falling")) s_r_ff_6 (
    .S(undriven_3), .clk(undriven_5), .R(undriven_4), .Q(s_r_ff_6_q), .reset(lcd_video_1_p8));  // open: Qn, preset, en
  S_R_Flip_Flop #(.trigger("falling")) s_r_ff_7 (
    .S(undriven_2), .clk(undriven_5), .R(undriven_4), .Q(s_r_ff_7_q), .reset(lcd_video_1_p8));  // open: Qn, preset, en
  Button REset_screen_2 (.out(lcd_video_1_p9));

  // Notes on the sheet:
  //   Instruction Counter
  //   Load From Register
  //   IR Clock On Falling Edge Can CAUSE ERRORS
  //   Reset Mem
  //   Reset Reg
  //   Is IR's clock on
  //   DONT FORGET TO SYNC IR WHEN STARTING A PROGRAM
  //   LoadFromMemory
  //   Enable sending to register
  //   THE IR CLOCK SHOULD TICK WHEN RAM's DOES THIS CAUSES ERRORS IN THE WHOLE COMPUTER(MCL, etc.)
  //   is ALU in use
  //   Copy Register
  //   FOR SOME REASON BACKWARDS LINES DOESNT WORK(A = (7f, 0), B = (0, 7f))
  //   Register File Input
  //   Register File Address
  //   Register A address
  //   Register B address
  //   Unsinged integer
  //   Register A Data
  //   Register B Data
  //   Greater Than
  //   EQual
  //   Less Than
  //   First 6 Bits Are OP Code Second 4 Bits Are Reg Addresses Third 4 Bits Also
  //   Fourth 8 Bits Are Unsigned Integer
  //   TODO(Probably not): Reset the reg file and the ram when rebooting
  //   THE SCREEN CANT HANDLE VALUES BIGGER THAN 127(DEC) AND THE SPLITTER REMOVES THE BIT FOR 128, 256, ETC.
  //   Greater Than
  //   EQual
  //   Less Than
  //   FOR THAT REASON IT CANT DISPLAY SOME LINES
endmodule

module RegisterBank (
  input  Write,
  input  [3:0] Select,
  input  [15:0] Input_Data,
  input  Clock,
  input  Master_Reset,
  input  [3:0] A_Select,
  input  [3:0] B_Select,
  output [15:0] A_Output,
  output [15:0] B_Output
);

  wire demultiplexer_1_out0, demultiplexer_1_out1, demultiplexer_1_out2, demultiplexer_1_out3,
       demultiplexer_1_out4, demultiplexer_1_out5, demultiplexer_1_out6, demultiplexer_1_out7,
       demultiplexer_1_out8, demultiplexer_1_out9, demultiplexer_1_out10, demultiplexer_1_out11,
       demultiplexer_1_out12, demultiplexer_1_out13, demultiplexer_1_out14, demultiplexer_1_out15;
  wire [15:0] Reg0_q, Reg1_q, Reg2_q, Reg3_q, Reg4_q, Reg5_q, Reg6_q, Reg7_q, Reg8_q, Reg9_q, RegA_q, RegB_q,
       RegC_q, RegD_q, RegE_q, RegF_q;

  Pull_Resistor pull_resistor_1 (.node(Clock));
  Pull_Resistor pull_resistor_2 (.node(Master_Reset));
  Register #(.width(16)) Reg0 (.D(Input_Data), .en(demultiplexer_1_out0), .Q(Reg0_q), .clk(Clock), .clr(Master_Reset));
  Register #(.width(16)) Reg1 (.D(Input_Data), .en(demultiplexer_1_out1), .Q(Reg1_q), .clk(Clock), .clr(Master_Reset));
  Multiplexer #(.select(4), .width(16), .enable("false")) multiplexer_1 (
    .in0(Reg0_q), .in1(Reg1_q), .in2(Reg2_q), .in3(Reg3_q), .in4(Reg4_q), .in5(Reg5_q), .in6(Reg6_q),
    .in7(Reg7_q), .in8(Reg8_q), .in9(Reg9_q), .in10(RegA_q), .in11(RegB_q), .in12(RegC_q), .in13(RegD_q),
    .in14(RegE_q), .in15(RegF_q), .out(A_Output), .sel(A_Select));
  Register #(.width(16)) Reg2 (.D(Input_Data), .en(demultiplexer_1_out2), .Q(Reg2_q), .clk(Clock), .clr(Master_Reset));
  Register #(.width(16)) Reg4 (.D(Input_Data), .en(demultiplexer_1_out4), .Q(Reg4_q), .clk(Clock), .clr(Master_Reset));
  Register #(.width(16)) Reg3 (.D(Input_Data), .en(demultiplexer_1_out3), .Q(Reg3_q), .clk(Clock), .clr(Master_Reset));
  Multiplexer #(.select(4), .width(16), .enable("false")) multiplexer_2 (
    .in0(Reg0_q), .in1(Reg1_q), .in2(Reg2_q), .in3(Reg3_q), .in4(Reg4_q), .in5(Reg5_q), .in6(Reg6_q),
    .in7(Reg7_q), .in8(Reg8_q), .in9(Reg9_q), .in10(RegA_q), .in11(RegB_q), .in12(RegC_q), .in13(RegD_q),
    .in14(RegE_q), .in15(RegF_q), .out(B_Output), .sel(B_Select));
  Register #(.width(16)) Reg5 (.D(Input_Data), .en(demultiplexer_1_out5), .Q(Reg5_q), .clk(Clock), .clr(Master_Reset));
  Register #(.width(16)) Reg6 (.D(Input_Data), .en(demultiplexer_1_out6), .Q(Reg6_q), .clk(Clock), .clr(Master_Reset));
  Demultiplexer #(.select(4), .disabled(0), .enable("false")) demultiplexer_1 (
    .out0(demultiplexer_1_out0), .out1(demultiplexer_1_out1), .out2(demultiplexer_1_out2),
    .out3(demultiplexer_1_out3), .out4(demultiplexer_1_out4), .out5(demultiplexer_1_out5),
    .out6(demultiplexer_1_out6), .out7(demultiplexer_1_out7), .out8(demultiplexer_1_out8),
    .out9(demultiplexer_1_out9), .out10(demultiplexer_1_out10), .out11(demultiplexer_1_out11),
    .out12(demultiplexer_1_out12), .out13(demultiplexer_1_out13), .out14(demultiplexer_1_out14),
    .out15(demultiplexer_1_out15), .in(Write), .sel(Select));
  Register #(.width(16)) Reg7 (.D(Input_Data), .en(demultiplexer_1_out7), .Q(Reg7_q), .clk(Clock), .clr(Master_Reset));
  Register #(.width(16)) Reg8 (.D(Input_Data), .en(demultiplexer_1_out8), .Q(Reg8_q), .clk(Clock), .clr(Master_Reset));
  Register #(.width(16)) Reg9 (.D(Input_Data), .en(demultiplexer_1_out9), .Q(Reg9_q), .clk(Clock), .clr(Master_Reset));
  Register #(.width(16)) RegA (.D(Input_Data), .en(demultiplexer_1_out10), .Q(RegA_q), .clk(Clock), .clr(Master_Reset));
  Register #(.width(16)) RegC (.D(Input_Data), .en(demultiplexer_1_out12), .Q(RegC_q), .clk(Clock), .clr(Master_Reset));
  Register #(.width(16)) RegB (.D(Input_Data), .en(demultiplexer_1_out11), .Q(RegB_q), .clk(Clock), .clr(Master_Reset));
  Register #(.width(16)) RegD (.D(Input_Data), .en(demultiplexer_1_out13), .Q(RegD_q), .clk(Clock), .clr(Master_Reset));
  Register #(.width(16)) RegE (.D(Input_Data), .en(demultiplexer_1_out14), .Q(RegE_q), .clk(Clock), .clr(Master_Reset));
  Register #(.width(16)) RegF (.D(Input_Data), .en(demultiplexer_1_out15), .Q(RegF_q), .clk(Clock), .clr(Master_Reset));

  // Notes on the sheet:
  //   Master_Reset: pull=down
  //   Clock: pull=down
endmodule

module ALU (
  input  [15:0] A,
  input  [15:0] B,
  input  [7:0] A_2,
  input  [7:0] B_2,
  input  [7:0] B_3,
  input  [3:0] Op_Code,
  input  Carry_Borrow,
  output C_Out,
  output B_Out,
  output [15:0] Output,
  output Negative,
  output Overflow,
  output Zero,
  output Greater_Than,
  output Equal,
  output Less_Than
);

  wire and_2_out, and_4_out, comparator_1_eq, comparator_1_gt, comparator_1_lt, NEgative_t;
  wire [3:0] OPCODE;
  wire [7:0] adder_2_out, subtractor_2_out;
  wire [15:0] adder_1_out, and_1_out, nand_1_out, nor_1_out, or_1_out, subtractor_1_out, xnor_1_out,
       xor_1_out;

  Pull_Resistor pull_resistor_1 (.node(A));
  Pull_Resistor pull_resistor_2 (.node(B));
  Pull_Resistor pull_resistor_3 (.node(Op_Code));
  Pull_Resistor pull_resistor_4 (.node(Carry_Borrow));
  Adder #(.width(16)) adder_1 (.a(A), .b(B), .out(adder_1_out), .cin(Carry_Borrow), .cout(C_Out));
  Subtractor #(.width(16)) subtractor_1 (.a(A), .b(B), .out(subtractor_1_out), .bin(Carry_Borrow), .bout(B_Out));
  assign and_1_out = A & B;  // AND_Gate and_1, 16 bits wide
  assign or_1_out = A | B;  // OR_Gate or_1, 16 bits wide
  assign xor_1_out = A ^ B;  // XOR_Gate xor_1, 16 bits wide
  assign nand_1_out = ~(A & B);  // NAND_Gate nand_1, 16 bits wide
  assign nor_1_out = ~(A | B);  // NOR_Gate nor_1, 16 bits wide
  assign xnor_1_out = ~(A ^ B);  // XNOR_Gate xnor_1, 16 bits wide
  Comparator #(.width(16)) comparator_1 (
    .a(A), .b(B), .gt(comparator_1_gt), .eq(comparator_1_eq), .lt(comparator_1_lt));
  Multiplexer #(.select(4), .width(16), .enable("false")) multiplexer_1 (
    .in0({16{1'b0}}), .in1(adder_1_out), .in2(subtractor_1_out), .in3(and_1_out), .in4(or_1_out),
    .in5(xor_1_out), .in6(nand_1_out), .in7(nor_1_out), .in8(xnor_1_out), .in9({16{1'b0}}),
    .in10({16{1'b0}}), .in11({16{1'b0}}), .in12({16{1'b0}}), .in13({16{1'b0}}), .in14({16{1'b0}}),
    .in15({16{1'b0}}), .out({Negative, Output[14:0]}), .sel(Op_Code));
  and and_2 (and_2_out, Op_Code[0], ~Op_Code[1], Op_Code[2], ~Op_Code[3]);  // AND_Gate
  and and_3 (Overflow, C_Out, Op_Code[0], ~Op_Code[1], ~Op_Code[2], ~Op_Code[3]);  // AND_Gate
  nor nor_2 (Zero, Output[0], Output[1], Output[2], Output[3], Output[4], Output[5], Output[6], Output[7], Output[8], Output[9], Output[10], Output[11], Output[12], Output[13], Output[14], Negative, Overflow);
  Transistor #(.\type ("n")) transistor_1 (.in(comparator_1_gt), .out(Greater_Than), .gate(and_2_out));
  Pull_Resistor pull_resistor_5 (.node(Greater_Than));
  Pull_Resistor pull_resistor_6 (.node(Equal));
  Transistor #(.\type ("n")) transistor_2 (.in(comparator_1_eq), .out(Equal), .gate(and_2_out));
  Transistor #(.\type ("n")) transistor_3 (.in(comparator_1_lt), .out(Less_Than), .gate(and_2_out));
  Pull_Resistor pull_resistor_7 (.node(Less_Than));
  Subtractor subtractor_2 (.a(A_2), .b(B_2), .out(subtractor_2_out));  // open: bin, bout
  Adder adder_2 (.a(subtractor_2_out), .b(B_3), .out(adder_2_out));  // open: cin, cout
  and and_4 (and_4_out, ~Zero, ~OPCODE[0], OPCODE[1], ~OPCODE[2], ~OPCODE[3]);  // AND_Gate
  and and_5 (NEgative_t, and_4_out, ~B_Out);  // AND_Gate

  assign Output[15] = Negative;

  // Other names for the same wires on the sheet: Bout = B_Out; Cout = C_Out; Ovrf = Overflow

  // Notes on the sheet:
  //   Flags
endmodule

module SAves (
  input  [3:0] Select,
  input  [15:0] Input_Data,
  input  Clock,
  input  Master_Reset,
  input  [3:0] A_Sel,
  input  [3:0] B_Sel,
  output [15:0] A_Out,
  output [15:0] B_Out
);

  wire decoder_1_out0, decoder_1_out1, decoder_1_out2, decoder_1_out3, decoder_1_out4, decoder_1_out5,
       decoder_1_out6, decoder_1_out7, decoder_1_out8, decoder_1_out9, decoder_1_out10, decoder_1_out11,
       decoder_1_out12, decoder_1_out13, decoder_1_out14, decoder_1_out15, undriven_17, undriven_18;
  wire [15:0] register_1_q, register_2_q, register_3_q, register_4_q, register_5_q, register_6_q,
       register_7_q, register_8_q, register_9_q, register_10_q, register_11_q, register_12_q, register_13_q,
       register_14_q, register_15_q, register_16_q, register_17_q, register_18_q, register_19_q,
       register_20_q, register_21_q, register_22_q, register_23_q, register_24_q, register_25_q,
       register_26_q, register_27_q, register_28_q, register_29_q, register_30_q, register_31_q,
       register_32_q, undriven, undriven_2, undriven_3, undriven_4, undriven_5, undriven_6, undriven_7,
       undriven_8, undriven_9, undriven_10, undriven_11, undriven_12, undriven_13, undriven_14, undriven_15,
       undriven_16;

  Register #(.width(16)) register_1 (
    .D(Input_Data), .en(decoder_1_out0), .Q(register_1_q), .clk(Clock), .clr(Master_Reset));
  Register #(.width(16)) register_2 (
    .D(Input_Data), .en(decoder_1_out1), .Q(register_2_q), .clk(Clock), .clr(Master_Reset));
  Register #(.width(16)) register_3 (
    .D(undriven_6), .Q(register_3_q), .clk(undriven_17), .clr(undriven_18));  // open: en
  Register #(.width(16)) register_4 (
    .D(Input_Data), .en(decoder_1_out2), .Q(register_4_q), .clk(Clock), .clr(Master_Reset));
  Register #(.width(16)) register_5 (.D(undriven), .Q(register_5_q), .clk(undriven_17), .clr(undriven_18));  // open: en
  Register #(.width(16)) register_6 (
    .D(Input_Data), .en(decoder_1_out3), .Q(register_6_q), .clk(Clock), .clr(Master_Reset));
  Register #(.width(16)) register_7 (
    .D(undriven_2), .Q(register_7_q), .clk(undriven_17), .clr(undriven_18));  // open: en
  Register #(.width(16)) register_8 (
    .D(Input_Data), .en(decoder_1_out4), .Q(register_8_q), .clk(Clock), .clr(Master_Reset));
  Register #(.width(16)) register_9 (
    .D(undriven_3), .Q(register_9_q), .clk(undriven_17), .clr(undriven_18));  // open: en
  Register #(.width(16)) register_10 (
    .D(undriven_7), .Q(register_10_q), .clk(undriven_17), .clr(undriven_18));  // open: en
  Decoder #(.select(4), .enable("false")) decoder_1 (
    .out0(decoder_1_out0), .out1(decoder_1_out1), .out2(decoder_1_out2), .out3(decoder_1_out3),
    .out4(decoder_1_out4), .out5(decoder_1_out5), .out6(decoder_1_out6), .out7(decoder_1_out7),
    .out8(decoder_1_out8), .out9(decoder_1_out9), .out10(decoder_1_out10), .out11(decoder_1_out11),
    .out12(decoder_1_out12), .out13(decoder_1_out13), .out14(decoder_1_out14), .out15(decoder_1_out15),
    .sel(Select));
  Register #(.width(16)) register_11 (
    .D(Input_Data), .en(decoder_1_out5), .Q(register_11_q), .clk(Clock), .clr(Master_Reset));
  Register #(.width(16)) register_12 (
    .D(Input_Data), .en(decoder_1_out6), .Q(register_12_q), .clk(Clock), .clr(Master_Reset));
  Register #(.width(16)) register_13 (
    .D(undriven_4), .Q(register_13_q), .clk(undriven_17), .clr(undriven_18));  // open: en
  Register #(.width(16)) register_14 (
    .D(Input_Data), .en(decoder_1_out7), .Q(register_14_q), .clk(Clock), .clr(Master_Reset));
  Register #(.width(16)) register_15 (
    .D(undriven_5), .Q(register_15_q), .clk(undriven_17), .clr(undriven_18));  // open: en
  Register #(.width(16)) register_16 (
    .D(Input_Data), .en(decoder_1_out8), .Q(register_16_q), .clk(Clock), .clr(Master_Reset));
  Multiplexer #(.select(4), .width(16)) multiplexer_1 (
    .in0(undriven_6), .in1(undriven), .in2(undriven_2), .in3(undriven_7), .in4(undriven_3), .in5(undriven_4),
    .in6(undriven_5), .in7(undriven_8), .in8(undriven_9), .in9(undriven_10), .in10(undriven_11),
    .in11(undriven_12), .in12(undriven_13), .in13(undriven_14), .in14(undriven_15), .in15(undriven_16));  // open: out, sel, en
  Register #(.width(16)) register_17 (
    .D(undriven_9), .Q(register_17_q), .clk(undriven_17), .clr(undriven_18));  // open: en
  Register #(.width(16)) register_18 (
    .D(undriven_8), .Q(register_18_q), .clk(undriven_17), .clr(undriven_18));  // open: en
  Register #(.width(16)) register_19 (
    .D(Input_Data), .en(decoder_1_out9), .Q(register_19_q), .clk(Clock), .clr(Master_Reset));
  Register #(.width(16)) register_20 (
    .D(undriven_10), .Q(register_20_q), .clk(undriven_17), .clr(undriven_18));  // open: en
  Register #(.width(16)) register_21 (
    .D(Input_Data), .en(decoder_1_out10), .Q(register_21_q), .clk(Clock), .clr(Master_Reset));
  Register #(.width(16)) register_22 (
    .D(undriven_11), .Q(register_22_q), .clk(undriven_17), .clr(undriven_18));  // open: en
  Register #(.width(16)) register_23 (
    .D(Input_Data), .en(decoder_1_out11), .Q(register_23_q), .clk(Clock), .clr(Master_Reset));
  Register #(.width(16)) register_24 (
    .D(undriven_13), .Q(register_24_q), .clk(undriven_17), .clr(undriven_18));  // open: en
  Register #(.width(16)) register_25 (
    .D(undriven_12), .Q(register_25_q), .clk(undriven_17), .clr(undriven_18));  // open: en
  Register #(.width(16)) register_26 (
    .D(Input_Data), .en(decoder_1_out12), .Q(register_26_q), .clk(Clock), .clr(Master_Reset));
  Register #(.width(16)) register_27 (
    .D(undriven_14), .Q(register_27_q), .clk(undriven_17), .clr(undriven_18));  // open: en
  Register #(.width(16)) register_28 (
    .D(Input_Data), .en(decoder_1_out14), .Q(register_28_q), .clk(Clock), .clr(Master_Reset));
  Register #(.width(16)) register_29 (
    .D(Input_Data), .en(decoder_1_out13), .Q(register_29_q), .clk(Clock), .clr(Master_Reset));
  Register #(.width(16)) register_30 (
    .D(undriven_15), .Q(register_30_q), .clk(undriven_17), .clr(undriven_18));  // open: en
  Register #(.width(16)) register_31 (
    .D(Input_Data), .en(decoder_1_out15), .Q(register_31_q), .clk(Clock), .clr(Master_Reset));
  Register #(.width(16)) register_32 (
    .D(undriven_16), .Q(register_32_q), .clk(undriven_17), .clr(undriven_18));  // open: en
  Multiplexer #(.select(4), .width(16), .enable("false")) multiplexer_2 (
    .in0(register_31_q), .in1(register_28_q), .in2(register_29_q), .in3(register_26_q), .in4(register_23_q),
    .in5(register_21_q), .in6(register_19_q), .in7(register_16_q), .in8(register_14_q), .in9(register_12_q),
    .in10(register_11_q), .in11(register_8_q), .in12(register_6_q), .in13(register_4_q), .in14(register_2_q),
    .in15(register_1_q), .out(A_Out), .sel(A_Sel));
  Multiplexer #(.select(4), .width(16), .enable("false")) multiplexer_3 (
    .in0(register_31_q), .in1(register_28_q), .in2(register_29_q), .in3(register_26_q), .in4(register_23_q),
    .in5(register_21_q), .in6(register_19_q), .in7(register_16_q), .in8(register_14_q), .in9(register_12_q),
    .in10(register_11_q), .in11(register_8_q), .in12(register_6_q), .in13(register_4_q), .in14(register_2_q),
    .in15(register_1_q), .out(B_Out), .sel(B_Sel));

  // Notes on the sheet:
  //   Clock: pull=down
  //   Master_Reset: pull=down
endmodule

module Decoder8Bit (
  input  [7:0] Select,
  input  [2:0] Select_2,
  output out_3,
  output out_4,
  output out_5,
  output out_6,
  output out_7,
  output out_8,
  output out_9,
  output out_10,
  output out_11,
  output out_12,
  output out_13,
  output out_14,
  output out_15,
  output out_16,
  output out_17,
  output out_18,
  output out_19,
  output out_20,
  output out_21,
  output out_22,
  output out_23,
  output out_24,
  output out_25,
  output out_26,
  output out_27,
  output out_28,
  output out_29,
  output out_30,
  output out_31,
  output out_32,
  output out_33,
  output out_34,
  output out_35,
  output out_36,
  output out_37,
  output out_38,
  output out_39,
  output out_40,
  output out_41,
  output out_42,
  output out_43,
  output out_44,
  output out_45,
  output out_46,
  output out_47,
  output out_48,
  output out_49,
  output out_50,
  output out_51,
  output out_52,
  output out_53,
  output out_54,
  output out_55,
  output out_56,
  output out_57,
  output out_58,
  output out_59,
  output out_60,
  output out_61,
  output out_62,
  output out_63,
  output out_64,
  output out_65,
  output out_66,
  output out_67,
  output out_68,
  output out_69,
  output out_70,
  output out_71,
  output out_72,
  output out_73,
  output out_74,
  output out_75,
  output out_76,
  output out_77,
  output out_78,
  output out_79,
  output out_80,
  output out_81,
  output out_82,
  output out_83,
  output out_84,
  output out_85,
  output out_86,
  output out_87,
  output out_88,
  output out_89,
  output out_90,
  output out_91,
  output out_92,
  output out_93,
  output out_94,
  output out_95,
  output out_96,
  output out_97,
  output out_98,
  output out_99,
  output out_100,
  output out_101,
  output out_102,
  output out_103,
  output out_104,
  output out_105,
  output out_106,
  output out_107,
  output out_108,
  output out_109,
  output out_110,
  output out_111,
  output out_112,
  output out_113,
  output out_114,
  output out_115,
  output out_116,
  output out_117,
  output out_118,
  output out_119,
  output out_120,
  output out_121,
  output out_122,
  output out_123,
  output out_124,
  output out_125,
  output out_126,
  output out_127,
  output out_128,
  output out_129,
  output out_130,
  output out_131,
  output out_132,
  output out_133,
  output out_134,
  output out_135,
  output out_136,
  output out_137,
  output out_138,
  output out_139,
  output out_140,
  output out_141,
  output out_142,
  output out_143,
  output out_144,
  output out_145,
  output out_146,
  output out_147,
  output out_148,
  output out_149,
  output out_150,
  output out_151,
  output out_152,
  output out_153,
  output out_154,
  output out_155,
  output out_156,
  output out_157,
  output out_158,
  output out_159,
  output out_160,
  output out_161,
  output out_162,
  output out_163,
  output out_164,
  output out_165,
  output out_166,
  output out_167,
  output out_168,
  output out_169,
  output out_170,
  output out_171,
  output out_172,
  output out_173,
  output out_174,
  output out_175,
  output out_176,
  output out_177,
  output out_178,
  output out_179,
  output out_180,
  output out_181,
  output out_182,
  output out_183,
  output out_184,
  output out_185,
  output out_186,
  output out_187,
  output out_188,
  output out_189,
  output out_190,
  output out_191,
  output out_192,
  output out_193,
  output out_194,
  output out_195,
  output out_196,
  output out_197,
  output out_198,
  output out_199,
  output out_200,
  output out_201,
  output out_202,
  output out_203,
  output out_204,
  output out_205,
  output out_206,
  output out_207,
  output out_208,
  output out_209,
  output out_210,
  output out_211,
  output out_212,
  output out_213,
  output out_214,
  output out_215,
  output out_216,
  output out_217,
  output out_218,
  output out_219,
  output out_220,
  output out_221,
  output out_222,
  output out_223,
  output out_224,
  output out_225,
  output out_226,
  output out_227,
  output out_228,
  output out_229,
  output out_230,
  output out_231,
  output out_232,
  output out_233,
  output out_234,
  output out_235,
  output out_236,
  output out_237,
  output out_238,
  output out_239,
  output out_240,
  output out_241,
  output out_242,
  output out_243,
  output out_244,
  output out_245,
  output out_246,
  output out_247,
  output out_248,
  output out_249,
  output out_250,
  output out_251,
  output out_252,
  output out_253,
  output out_254,
  output out_255,
  output out_256,
  output out_257,
  output out_258
);

  wire decoder_1_out0, decoder_1_out1, decoder_1_out2, decoder_1_out3, decoder_1_out4, decoder_1_out5,
       decoder_1_out6, decoder_1_out7, decoder_10_out0, decoder_10_out1, decoder_10_out2, decoder_10_out3,
       decoder_11_out0, decoder_11_out1, decoder_11_out2, decoder_11_out3, not_1_out;

  Decoder #(.select(3), .disabled(0), .enable("false")) decoder_1 (
    .out0(decoder_1_out0), .out1(decoder_1_out1), .out2(decoder_1_out2), .out3(decoder_1_out3),
    .out4(decoder_1_out4), .out5(decoder_1_out5), .out6(decoder_1_out6), .out7(decoder_1_out7),
    .sel(Select[7:5]));
  Decoder #(.select(5), .disabled(0)) decoder_2 (
    .out0(out_3), .out1(out_4), .out2(out_5), .out3(out_6), .out4(out_7), .out5(out_8), .out6(out_9),
    .out7(out_10), .out8(out_11), .out9(out_12), .out10(out_13), .out11(out_14), .out12(out_15),
    .out13(out_16), .out14(out_17), .out15(out_18), .out16(out_19), .out17(out_20), .out18(out_21),
    .out19(out_22), .out20(out_23), .out21(out_24), .out22(out_25), .out23(out_26), .out24(out_27),
    .out25(out_28), .out26(out_29), .out27(out_30), .out28(out_31), .out29(out_32), .out30(out_33),
    .out31(out_34), .sel(Select[4:0]), .en(decoder_1_out0));
  Decoder #(.select(5), .disabled(0)) decoder_3 (
    .out0(out_35), .out1(out_36), .out2(out_37), .out3(out_38), .out4(out_39), .out5(out_40), .out6(out_41),
    .out7(out_42), .out8(out_43), .out9(out_44), .out10(out_45), .out11(out_46), .out12(out_47),
    .out13(out_48), .out14(out_49), .out15(out_50), .out16(out_51), .out17(out_52), .out18(out_53),
    .out19(out_54), .out20(out_55), .out21(out_56), .out22(out_57), .out23(out_58), .out24(out_59),
    .out25(out_60), .out26(out_61), .out27(out_62), .out28(out_63), .out29(out_64), .out30(out_65),
    .out31(out_66), .sel(Select[4:0]), .en(decoder_1_out1));
  Decoder #(.select(5), .disabled(0)) decoder_4 (
    .out0(out_67), .out1(out_68), .out2(out_69), .out3(out_70), .out4(out_71), .out5(out_72), .out6(out_73),
    .out7(out_74), .out8(out_75), .out9(out_76), .out10(out_77), .out11(out_78), .out12(out_79),
    .out13(out_80), .out14(out_81), .out15(out_82), .out16(out_83), .out17(out_84), .out18(out_85),
    .out19(out_86), .out20(out_87), .out21(out_88), .out22(out_89), .out23(out_90), .out24(out_91),
    .out25(out_92), .out26(out_93), .out27(out_94), .out28(out_95), .out29(out_96), .out30(out_97),
    .out31(out_98), .sel(Select[4:0]), .en(decoder_1_out2));
  Decoder #(.select(5), .disabled(0)) decoder_5 (
    .out0(out_99), .out1(out_100), .out2(out_101), .out3(out_102), .out4(out_103), .out5(out_104),
    .out6(out_105), .out7(out_106), .out8(out_107), .out9(out_108), .out10(out_109), .out11(out_110),
    .out12(out_111), .out13(out_112), .out14(out_113), .out15(out_114), .out16(out_115), .out17(out_116),
    .out18(out_117), .out19(out_118), .out20(out_119), .out21(out_120), .out22(out_121), .out23(out_122),
    .out24(out_123), .out25(out_124), .out26(out_125), .out27(out_126), .out28(out_127), .out29(out_128),
    .out30(out_129), .out31(out_130), .sel(Select[4:0]), .en(decoder_1_out3));
  Decoder #(.select(5), .disabled(0)) decoder_6 (
    .out0(out_131), .out1(out_132), .out2(out_133), .out3(out_134), .out4(out_135), .out5(out_136),
    .out6(out_137), .out7(out_138), .out8(out_139), .out9(out_140), .out10(out_141), .out11(out_142),
    .out12(out_143), .out13(out_144), .out14(out_145), .out15(out_146), .out16(out_147), .out17(out_148),
    .out18(out_149), .out19(out_150), .out20(out_151), .out21(out_152), .out22(out_153), .out23(out_154),
    .out24(out_155), .out25(out_156), .out26(out_157), .out27(out_158), .out28(out_159), .out29(out_160),
    .out30(out_161), .out31(out_162), .sel(Select[4:0]), .en(decoder_1_out4));
  Decoder #(.select(5), .disabled(0)) decoder_7 (
    .out0(out_163), .out1(out_164), .out2(out_165), .out3(out_166), .out4(out_167), .out5(out_168),
    .out6(out_169), .out7(out_170), .out8(out_171), .out9(out_172), .out10(out_173), .out11(out_174),
    .out12(out_175), .out13(out_176), .out14(out_177), .out15(out_178), .out16(out_179), .out17(out_180),
    .out18(out_181), .out19(out_182), .out20(out_183), .out21(out_184), .out22(out_185), .out23(out_186),
    .out24(out_187), .out25(out_188), .out26(out_189), .out27(out_190), .out28(out_191), .out29(out_192),
    .out30(out_193), .out31(out_194), .sel(Select[4:0]), .en(decoder_1_out5));
  Decoder #(.select(5), .disabled(0)) decoder_8 (
    .out0(out_195), .out1(out_196), .out2(out_197), .out3(out_198), .out4(out_199), .out5(out_200),
    .out6(out_201), .out7(out_202), .out8(out_203), .out9(out_204), .out10(out_205), .out11(out_206),
    .out12(out_207), .out13(out_208), .out14(out_209), .out15(out_210), .out16(out_211), .out17(out_212),
    .out18(out_213), .out19(out_214), .out20(out_215), .out21(out_216), .out22(out_217), .out23(out_218),
    .out24(out_219), .out25(out_220), .out26(out_221), .out27(out_222), .out28(out_223), .out29(out_224),
    .out30(out_225), .out31(out_226), .sel(Select[4:0]), .en(decoder_1_out6));
  Decoder #(.select(5), .disabled(0)) decoder_9 (
    .out0(out_227), .out1(out_228), .out2(out_229), .out3(out_230), .out4(out_231), .out5(out_232),
    .out6(out_233), .out7(out_234), .out8(out_235), .out9(out_236), .out10(out_237), .out11(out_238),
    .out12(out_239), .out13(out_240), .out14(out_241), .out15(out_242), .out16(out_243), .out17(out_244),
    .out18(out_245), .out19(out_246), .out20(out_247), .out21(out_248), .out22(out_249), .out23(out_250),
    .out24(out_251), .out25(out_252), .out26(out_253), .out27(out_254), .out28(out_255), .out29(out_256),
    .out30(out_257), .out31(out_258), .sel(Select[4:0]), .en(decoder_1_out7));
  not not_1 (not_1_out, Select_2[2]);
  Decoder #(.select(2), .disabled(0)) decoder_10 (
    .out0(decoder_10_out0), .out1(decoder_10_out1), .out2(decoder_10_out2), .out3(decoder_10_out3),
    .sel(Select_2[1:0]), .en(not_1_out));
  Decoder #(.select(2), .disabled(0)) decoder_11 (
    .out0(decoder_11_out0), .out1(decoder_11_out1), .out2(decoder_11_out2), .out3(decoder_11_out3),
    .sel(Select_2[1:0]), .en(Select_2[2]));
endmodule

module Decoder6Bit (
  input  [5:0] Select,
  output out_2,
  output out_3,
  output out_4,
  output out_5,
  output out_6,
  output out_7,
  output out_8,
  output out_9,
  output out_10,
  output out_11,
  output out_12,
  output out_13,
  output out_14,
  output out_15,
  output out_16,
  output out_17,
  output out_18,
  output out_19,
  output out_20,
  output out_21,
  output out_22,
  output out_23,
  output out_24,
  output out_25,
  output out_26,
  output out_27,
  output out_28,
  output out_29,
  output out_30,
  output out_31,
  output out_32,
  output out_33,
  output out_34,
  output out_35,
  output out_36,
  output out_37,
  output out_38,
  output out_39,
  output out_40,
  output out_41,
  output out_42,
  output out_43,
  output out_44,
  output out_45,
  output out_46,
  output out_47,
  output out_48,
  output out_49,
  output out_50,
  output out_51,
  output out_52,
  output out_53,
  output out_54,
  output out_55,
  output out_56,
  output out_57,
  output out_58,
  output out_59,
  output out_60,
  output out_61,
  output out_62,
  output out_63,
  output out_64,
  output out_65
);

  wire not_1_out;

  Pull_Resistor pull_resistor_1 (.node(Select));
  Decoder #(.select(5), .disabled(0)) decoder_1 (
    .out0(out_2), .out1(out_3), .out2(out_4), .out3(out_5), .out4(out_6), .out5(out_7), .out6(out_8),
    .out7(out_9), .out8(out_10), .out9(out_11), .out10(out_12), .out11(out_13), .out12(out_14),
    .out13(out_15), .out14(out_16), .out15(out_17), .out16(out_18), .out17(out_19), .out18(out_20),
    .out19(out_21), .out20(out_22), .out21(out_23), .out22(out_24), .out23(out_25), .out24(out_26),
    .out25(out_27), .out26(out_28), .out27(out_29), .out28(out_30), .out29(out_31), .out30(out_32),
    .out31(out_33), .sel(Select[4:0]), .en(not_1_out));
  not not_1 (not_1_out, Select[5]);
  Decoder #(.select(5), .disabled(0)) decoder_2 (
    .out0(out_34), .out1(out_35), .out2(out_36), .out3(out_37), .out4(out_38), .out5(out_39), .out6(out_40),
    .out7(out_41), .out8(out_42), .out9(out_43), .out10(out_44), .out11(out_45), .out12(out_46),
    .out13(out_47), .out14(out_48), .out15(out_49), .out16(out_50), .out17(out_51), .out18(out_52),
    .out19(out_53), .out20(out_54), .out21(out_55), .out22(out_56), .out23(out_57), .out24(out_58),
    .out25(out_59), .out26(out_60), .out27(out_61), .out28(out_62), .out29(out_63), .out30(out_64),
    .out31(out_65), .sel(Select[4:0]), .en(Select[5]));
endmodule

module _22BitNOR (
  input  [21:0] in_1,
  output out_2
);

  nor nor_1 (out_2, in_1[0], in_1[1], in_1[2], in_1[3], in_1[4], in_1[5], in_1[6], in_1[7], in_1[8], in_1[9], in_1[10], in_1[11], in_1[12], in_1[13], in_1[14], in_1[15], in_1[16], in_1[17], in_1[18], in_1[19], in_1[20], in_1[21]);
endmodule

module XYToMatrix32 (
  input  [4:0] X,
  input  [4:0] Y,
  input  write,
  input  clear,
  input  clock,
  output [31:0] out_6,
  output [31:0] out_7,
  output [31:0] out_8,
  output [31:0] out_9,
  output [31:0] out_10,
  output [31:0] out_11,
  output [31:0] out_12,
  output [31:0] out_13,
  output [31:0] out_14,
  output [31:0] out_15,
  output [31:0] out_16,
  output [31:0] out_17,
  output [31:0] out_18,
  output [31:0] out_19,
  output [31:0] out_20,
  output [31:0] out_21,
  output [31:0] out_22,
  output [31:0] out_23,
  output [31:0] out_24,
  output [31:0] out_25,
  output [31:0] out_26,
  output [31:0] out_27,
  output [31:0] out_28,
  output [31:0] out_29,
  output [31:0] out_30,
  output [31:0] out_31,
  output [31:0] out_32,
  output [31:0] out_33,
  output [31:0] out_34,
  output [31:0] out_35,
  output [31:0] out_36,
  output [31:0] out_37
);

  wire comparator_1_eq, comparator_2_eq, comparator_3_eq, comparator_4_eq, comparator_5_eq, comparator_6_eq,
       comparator_7_eq, comparator_8_eq, comparator_9_eq, comparator_10_eq, comparator_11_eq,
       comparator_12_eq, comparator_13_eq, comparator_14_eq, comparator_15_eq, comparator_16_eq,
       comparator_17_eq, comparator_18_eq, comparator_19_eq, comparator_20_eq, comparator_21_eq,
       comparator_22_eq, comparator_23_eq, comparator_24_eq, comparator_25_eq, comparator_26_eq,
       comparator_27_eq, comparator_28_eq, comparator_29_eq, comparator_30_eq, comparator_31_eq,
       comparator_32_eq, or_1_out;
  wire [31:0] and_1_out, and_2_out, and_3_out, and_4_out, and_5_out, and_6_out, and_7_out, and_8_out,
       and_9_out, and_10_out, and_11_out, and_12_out, and_13_out, and_14_out, and_15_out, and_16_out,
       and_17_out, and_18_out, and_19_out, and_20_out, and_21_out, and_22_out, and_23_out, and_24_out,
       and_25_out, and_26_out, and_27_out, and_28_out, and_29_out, and_30_out, and_31_out, and_32_out,
       and_33_out, and_34_out, and_35_out, and_36_out, and_37_out, and_38_out, and_39_out, and_40_out,
       and_41_out, and_42_out, and_43_out, and_44_out, and_45_out, and_46_out, and_47_out, and_48_out,
       and_49_out, and_50_out, and_51_out, and_52_out, and_53_out, and_54_out, and_55_out, and_56_out,
       and_57_out, and_58_out, and_59_out, and_60_out, and_61_out, and_62_out, and_63_out, and_64_out,
       bit_extender_1_out, bit_extender_2_out, bit_extender_3_out, bit_extender_4_out, bit_extender_5_out,
       bit_extender_6_out, bit_extender_7_out, bit_extender_8_out, bit_extender_9_out, bit_extender_10_out,
       bit_extender_11_out, bit_extender_12_out, bit_extender_13_out, bit_extender_14_out,
       bit_extender_15_out, bit_extender_16_out, bit_extender_17_out, bit_extender_18_out,
       bit_extender_19_out, bit_extender_20_out, bit_extender_21_out, bit_extender_22_out,
       bit_extender_23_out, bit_extender_24_out, bit_extender_25_out, bit_extender_26_out,
       bit_extender_27_out, bit_extender_28_out, bit_extender_29_out, bit_extender_30_out,
       bit_extender_31_out, bit_extender_32_out, bit_extender_33_out, or_2_out, or_3_out, or_4_out, or_5_out,
       or_6_out, or_7_out, or_8_out, or_9_out, or_10_out, or_11_out, or_12_out, or_13_out, or_14_out,
       or_15_out, or_16_out, or_17_out, or_18_out, or_19_out, or_20_out, or_21_out, or_22_out, or_23_out,
       or_24_out, or_25_out, or_26_out, or_27_out, or_28_out, or_29_out, or_30_out, or_31_out, or_32_out,
       or_33_out, shifter_1_out;

  assign bit_extender_1_out = {{31{clear}}, clear};  // Bit_Extender bit_extender_1
  Shifter #(.width(32)) shifter_1 (.in(32'h1), .\dist (Y), .out(shifter_1_out));
  or or_1 (or_1_out, write, clear);
  Comparator #(.width(5)) comparator_1 (.a({5{1'b0}}), .b(X), .eq(comparator_1_eq));  // open: gt, lt
  assign bit_extender_2_out = {{31{comparator_1_eq}}, comparator_1_eq};  // Bit_Extender bit_extender_2
  Comparator #(.width(5)) comparator_2 (.a(5'b00001), .b(X), .eq(comparator_2_eq));  // open: gt, lt
  assign bit_extender_3_out = {{31{comparator_2_eq}}, comparator_2_eq};  // Bit_Extender bit_extender_3
  assign bit_extender_4_out = {{31{comparator_3_eq}}, comparator_3_eq};  // Bit_Extender bit_extender_4
  Comparator #(.width(5)) comparator_3 (.a(5'b00010), .b(X), .eq(comparator_3_eq));  // open: gt, lt
  assign bit_extender_5_out = {{31{comparator_4_eq}}, comparator_4_eq};  // Bit_Extender bit_extender_5
  Comparator #(.width(5)) comparator_4 (.a(5'b00011), .b(X), .eq(comparator_4_eq));  // open: gt, lt
  assign bit_extender_6_out = {{31{comparator_5_eq}}, comparator_5_eq};  // Bit_Extender bit_extender_6
  Comparator #(.width(5)) comparator_5 (.a(5'b00100), .b(X), .eq(comparator_5_eq));  // open: gt, lt
  Comparator #(.width(5)) comparator_6 (.a(5'b00101), .b(X), .eq(comparator_6_eq));  // open: gt, lt
  assign bit_extender_7_out = {{31{comparator_6_eq}}, comparator_6_eq};  // Bit_Extender bit_extender_7
  Comparator #(.width(5)) comparator_7 (.a(5'b00110), .b(X), .eq(comparator_7_eq));  // open: gt, lt
  assign bit_extender_8_out = {{31{comparator_7_eq}}, comparator_7_eq};  // Bit_Extender bit_extender_8
  Comparator #(.width(5)) comparator_8 (.a(5'b00111), .b(X), .eq(comparator_8_eq));  // open: gt, lt
  assign bit_extender_9_out = {{31{comparator_8_eq}}, comparator_8_eq};  // Bit_Extender bit_extender_9
  assign bit_extender_10_out = {{31{comparator_9_eq}}, comparator_9_eq};  // Bit_Extender bit_extender_10
  Comparator #(.width(5)) comparator_9 (.a(5'b01000), .b(X), .eq(comparator_9_eq));  // open: gt, lt
  Comparator #(.width(5)) comparator_10 (.a(5'b01001), .b(X), .eq(comparator_10_eq));  // open: gt, lt
  assign bit_extender_11_out = {{31{comparator_10_eq}}, comparator_10_eq};  // Bit_Extender bit_extender_11
  Comparator #(.width(5)) comparator_11 (.a(5'b01010), .b(X), .eq(comparator_11_eq));  // open: gt, lt
  assign bit_extender_12_out = {{31{comparator_11_eq}}, comparator_11_eq};  // Bit_Extender bit_extender_12
  Comparator #(.width(5)) comparator_12 (.a(5'b01011), .b(X), .eq(comparator_12_eq));  // open: gt, lt
  assign bit_extender_13_out = {{31{comparator_12_eq}}, comparator_12_eq};  // Bit_Extender bit_extender_13
  assign bit_extender_14_out = {{31{comparator_13_eq}}, comparator_13_eq};  // Bit_Extender bit_extender_14
  Comparator #(.width(5)) comparator_13 (.a(5'b01100), .b(X), .eq(comparator_13_eq));  // open: gt, lt
  assign bit_extender_15_out = {{31{comparator_14_eq}}, comparator_14_eq};  // Bit_Extender bit_extender_15
  Comparator #(.width(5)) comparator_14 (.a(5'b01101), .b(X), .eq(comparator_14_eq));  // open: gt, lt
  assign bit_extender_16_out = {{31{comparator_15_eq}}, comparator_15_eq};  // Bit_Extender bit_extender_16
  Comparator #(.width(5)) comparator_15 (.a(5'b01110), .b(X), .eq(comparator_15_eq));  // open: gt, lt
  Comparator #(.width(5)) comparator_16 (.a(5'b01111), .b(X), .eq(comparator_16_eq));  // open: gt, lt
  assign bit_extender_17_out = {{31{comparator_16_eq}}, comparator_16_eq};  // Bit_Extender bit_extender_17
  Comparator #(.width(5)) comparator_17 (.a(5'b10000), .b(X), .eq(comparator_17_eq));  // open: gt, lt
  assign bit_extender_18_out = {{31{comparator_17_eq}}, comparator_17_eq};  // Bit_Extender bit_extender_18
  assign bit_extender_19_out = {{31{comparator_18_eq}}, comparator_18_eq};  // Bit_Extender bit_extender_19
  Comparator #(.width(5)) comparator_18 (.a(5'b10001), .b(X), .eq(comparator_18_eq));  // open: gt, lt
  Comparator #(.width(5)) comparator_19 (.a(5'b10010), .b(X), .eq(comparator_19_eq));  // open: gt, lt
  assign bit_extender_20_out = {{31{comparator_19_eq}}, comparator_19_eq};  // Bit_Extender bit_extender_20
  assign bit_extender_21_out = {{31{comparator_20_eq}}, comparator_20_eq};  // Bit_Extender bit_extender_21
  Comparator #(.width(5)) comparator_20 (.a(5'b10011), .b(X), .eq(comparator_20_eq));  // open: gt, lt
  Comparator #(.width(5)) comparator_21 (.a(5'b10100), .b(X), .eq(comparator_21_eq));  // open: gt, lt
  assign bit_extender_22_out = {{31{comparator_21_eq}}, comparator_21_eq};  // Bit_Extender bit_extender_22
  Comparator #(.width(5)) comparator_22 (.a(5'b10101), .b(X), .eq(comparator_22_eq));  // open: gt, lt
  assign bit_extender_23_out = {{31{comparator_22_eq}}, comparator_22_eq};  // Bit_Extender bit_extender_23
  assign bit_extender_24_out = {{31{comparator_23_eq}}, comparator_23_eq};  // Bit_Extender bit_extender_24
  Comparator #(.width(5)) comparator_23 (.a(5'b10110), .b(X), .eq(comparator_23_eq));  // open: gt, lt
  Comparator #(.width(5)) comparator_24 (.a(5'b10111), .b(X), .eq(comparator_24_eq));  // open: gt, lt
  assign bit_extender_25_out = {{31{comparator_24_eq}}, comparator_24_eq};  // Bit_Extender bit_extender_25
  assign bit_extender_26_out = {{31{comparator_25_eq}}, comparator_25_eq};  // Bit_Extender bit_extender_26
  Comparator #(.width(5)) comparator_25 (.a(5'b11000), .b(X), .eq(comparator_25_eq));  // open: gt, lt
  Comparator #(.width(5)) comparator_26 (.a(5'b11001), .b(X), .eq(comparator_26_eq));  // open: gt, lt
  assign bit_extender_27_out = {{31{comparator_26_eq}}, comparator_26_eq};  // Bit_Extender bit_extender_27
  Comparator #(.width(5)) comparator_27 (.a(5'b11010), .b(X), .eq(comparator_27_eq));  // open: gt, lt
  assign bit_extender_28_out = {{31{comparator_27_eq}}, comparator_27_eq};  // Bit_Extender bit_extender_28
  Comparator #(.width(5)) comparator_28 (.a(5'b11011), .b(X), .eq(comparator_28_eq));  // open: gt, lt
  assign bit_extender_29_out = {{31{comparator_28_eq}}, comparator_28_eq};  // Bit_Extender bit_extender_29
  Comparator #(.width(5)) comparator_29 (.a(5'b11100), .b(X), .eq(comparator_29_eq));  // open: gt, lt
  assign bit_extender_30_out = {{31{comparator_29_eq}}, comparator_29_eq};  // Bit_Extender bit_extender_30
  Comparator #(.width(5)) comparator_30 (.a(5'b11101), .b(X), .eq(comparator_30_eq));  // open: gt, lt
  assign bit_extender_31_out = {{31{comparator_30_eq}}, comparator_30_eq};  // Bit_Extender bit_extender_31
  assign bit_extender_32_out = {{31{comparator_31_eq}}, comparator_31_eq};  // Bit_Extender bit_extender_32
  Comparator #(.width(5)) comparator_31 (.a(5'b11110), .b(X), .eq(comparator_31_eq));  // open: gt, lt
  assign bit_extender_33_out = {{31{comparator_32_eq}}, comparator_32_eq};  // Bit_Extender bit_extender_33
  Comparator #(.width(5)) comparator_32 (.a({5{1'b1}}), .b(X), .eq(comparator_32_eq));  // open: gt, lt
  assign and_1_out = bit_extender_2_out & shifter_1_out;  // AND_Gate and_1, 32 bits wide
  assign or_2_out = and_1_out | out_6;  // OR_Gate or_2, 32 bits wide
  assign and_2_out = bit_extender_3_out & shifter_1_out;  // AND_Gate and_2, 32 bits wide
  assign or_3_out = and_2_out | out_7;  // OR_Gate or_3, 32 bits wide
  assign and_3_out = bit_extender_4_out & shifter_1_out;  // AND_Gate and_3, 32 bits wide
  assign or_4_out = and_3_out | out_8;  // OR_Gate or_4, 32 bits wide
  assign and_4_out = bit_extender_5_out & shifter_1_out;  // AND_Gate and_4, 32 bits wide
  assign or_5_out = and_4_out | out_9;  // OR_Gate or_5, 32 bits wide
  assign and_5_out = bit_extender_6_out & shifter_1_out;  // AND_Gate and_5, 32 bits wide
  assign or_6_out = and_5_out | out_10;  // OR_Gate or_6, 32 bits wide
  assign and_6_out = bit_extender_7_out & shifter_1_out;  // AND_Gate and_6, 32 bits wide
  assign or_7_out = and_6_out | out_11;  // OR_Gate or_7, 32 bits wide
  assign and_7_out = bit_extender_8_out & shifter_1_out;  // AND_Gate and_7, 32 bits wide
  assign or_8_out = and_7_out | out_12;  // OR_Gate or_8, 32 bits wide
  assign and_8_out = bit_extender_9_out & shifter_1_out;  // AND_Gate and_8, 32 bits wide
  assign or_9_out = and_8_out | out_13;  // OR_Gate or_9, 32 bits wide
  assign and_9_out = bit_extender_10_out & shifter_1_out;  // AND_Gate and_9, 32 bits wide
  assign or_10_out = and_9_out | out_14;  // OR_Gate or_10, 32 bits wide
  assign and_10_out = bit_extender_11_out & shifter_1_out;  // AND_Gate and_10, 32 bits wide
  assign or_11_out = and_10_out | out_15;  // OR_Gate or_11, 32 bits wide
  assign and_11_out = bit_extender_12_out & shifter_1_out;  // AND_Gate and_11, 32 bits wide
  assign or_12_out = and_11_out | out_16;  // OR_Gate or_12, 32 bits wide
  assign and_12_out = bit_extender_13_out & shifter_1_out;  // AND_Gate and_12, 32 bits wide
  assign or_13_out = and_12_out | out_17;  // OR_Gate or_13, 32 bits wide
  assign and_13_out = bit_extender_14_out & shifter_1_out;  // AND_Gate and_13, 32 bits wide
  assign or_14_out = and_13_out | out_18;  // OR_Gate or_14, 32 bits wide
  assign and_14_out = bit_extender_15_out & shifter_1_out;  // AND_Gate and_14, 32 bits wide
  assign or_15_out = and_14_out | out_19;  // OR_Gate or_15, 32 bits wide
  assign and_15_out = bit_extender_16_out & shifter_1_out;  // AND_Gate and_15, 32 bits wide
  assign or_16_out = and_15_out | out_20;  // OR_Gate or_16, 32 bits wide
  assign and_16_out = bit_extender_17_out & shifter_1_out;  // AND_Gate and_16, 32 bits wide
  assign or_17_out = and_16_out | out_21;  // OR_Gate or_17, 32 bits wide
  assign and_17_out = bit_extender_18_out & shifter_1_out;  // AND_Gate and_17, 32 bits wide
  assign or_18_out = and_17_out | out_22;  // OR_Gate or_18, 32 bits wide
  assign and_18_out = bit_extender_19_out & shifter_1_out;  // AND_Gate and_18, 32 bits wide
  assign or_19_out = and_18_out | out_23;  // OR_Gate or_19, 32 bits wide
  assign and_19_out = bit_extender_20_out & shifter_1_out;  // AND_Gate and_19, 32 bits wide
  assign or_20_out = and_19_out | out_24;  // OR_Gate or_20, 32 bits wide
  assign and_20_out = bit_extender_21_out & shifter_1_out;  // AND_Gate and_20, 32 bits wide
  assign or_21_out = and_20_out | out_25;  // OR_Gate or_21, 32 bits wide
  assign and_21_out = bit_extender_22_out & shifter_1_out;  // AND_Gate and_21, 32 bits wide
  assign or_22_out = and_21_out | out_26;  // OR_Gate or_22, 32 bits wide
  assign and_22_out = bit_extender_23_out & shifter_1_out;  // AND_Gate and_22, 32 bits wide
  assign or_23_out = and_22_out | out_27;  // OR_Gate or_23, 32 bits wide
  assign and_23_out = bit_extender_24_out & shifter_1_out;  // AND_Gate and_23, 32 bits wide
  assign or_24_out = and_23_out | out_28;  // OR_Gate or_24, 32 bits wide
  assign and_24_out = bit_extender_25_out & shifter_1_out;  // AND_Gate and_24, 32 bits wide
  assign or_25_out = and_24_out | out_29;  // OR_Gate or_25, 32 bits wide
  assign and_25_out = bit_extender_26_out & shifter_1_out;  // AND_Gate and_25, 32 bits wide
  assign or_26_out = and_25_out | out_30;  // OR_Gate or_26, 32 bits wide
  assign and_26_out = bit_extender_27_out & shifter_1_out;  // AND_Gate and_26, 32 bits wide
  assign or_27_out = and_26_out | out_31;  // OR_Gate or_27, 32 bits wide
  assign and_27_out = bit_extender_28_out & shifter_1_out;  // AND_Gate and_27, 32 bits wide
  assign or_28_out = and_27_out | out_32;  // OR_Gate or_28, 32 bits wide
  assign and_28_out = bit_extender_29_out & shifter_1_out;  // AND_Gate and_28, 32 bits wide
  assign or_29_out = and_28_out | out_33;  // OR_Gate or_29, 32 bits wide
  assign and_29_out = bit_extender_30_out & shifter_1_out;  // AND_Gate and_29, 32 bits wide
  assign or_30_out = and_29_out | out_34;  // OR_Gate or_30, 32 bits wide
  assign and_30_out = bit_extender_31_out & shifter_1_out;  // AND_Gate and_30, 32 bits wide
  assign or_31_out = and_30_out | out_35;  // OR_Gate or_31, 32 bits wide
  assign and_31_out = bit_extender_32_out & shifter_1_out;  // AND_Gate and_31, 32 bits wide
  assign or_32_out = and_31_out | out_36;  // OR_Gate or_32, 32 bits wide
  assign and_32_out = bit_extender_33_out & shifter_1_out;  // AND_Gate and_32, 32 bits wide
  assign or_33_out = and_32_out | out_37;  // OR_Gate or_33, 32 bits wide
  assign and_33_out = or_2_out & ~bit_extender_1_out;  // AND_Gate and_33, 32 bits wide
  assign and_34_out = or_3_out & ~bit_extender_1_out;  // AND_Gate and_34, 32 bits wide
  assign and_35_out = or_4_out & ~bit_extender_1_out;  // AND_Gate and_35, 32 bits wide
  assign and_36_out = or_5_out & ~bit_extender_1_out;  // AND_Gate and_36, 32 bits wide
  assign and_37_out = or_6_out & ~bit_extender_1_out;  // AND_Gate and_37, 32 bits wide
  assign and_38_out = or_7_out & ~bit_extender_1_out;  // AND_Gate and_38, 32 bits wide
  assign and_39_out = or_8_out & ~bit_extender_1_out;  // AND_Gate and_39, 32 bits wide
  assign and_40_out = or_9_out & ~bit_extender_1_out;  // AND_Gate and_40, 32 bits wide
  assign and_41_out = or_10_out & ~bit_extender_1_out;  // AND_Gate and_41, 32 bits wide
  assign and_42_out = or_11_out & ~bit_extender_1_out;  // AND_Gate and_42, 32 bits wide
  assign and_43_out = or_12_out & ~bit_extender_1_out;  // AND_Gate and_43, 32 bits wide
  assign and_44_out = or_13_out & ~bit_extender_1_out;  // AND_Gate and_44, 32 bits wide
  assign and_45_out = or_14_out & ~bit_extender_1_out;  // AND_Gate and_45, 32 bits wide
  assign and_46_out = or_15_out & ~bit_extender_1_out;  // AND_Gate and_46, 32 bits wide
  assign and_47_out = or_16_out & ~bit_extender_1_out;  // AND_Gate and_47, 32 bits wide
  assign and_48_out = or_17_out & ~bit_extender_1_out;  // AND_Gate and_48, 32 bits wide
  assign and_49_out = or_18_out & ~bit_extender_1_out;  // AND_Gate and_49, 32 bits wide
  assign and_50_out = or_19_out & ~bit_extender_1_out;  // AND_Gate and_50, 32 bits wide
  assign and_51_out = or_20_out & ~bit_extender_1_out;  // AND_Gate and_51, 32 bits wide
  assign and_52_out = or_21_out & ~bit_extender_1_out;  // AND_Gate and_52, 32 bits wide
  assign and_53_out = or_22_out & ~bit_extender_1_out;  // AND_Gate and_53, 32 bits wide
  assign and_54_out = or_23_out & ~bit_extender_1_out;  // AND_Gate and_54, 32 bits wide
  assign and_55_out = or_24_out & ~bit_extender_1_out;  // AND_Gate and_55, 32 bits wide
  assign and_56_out = or_25_out & ~bit_extender_1_out;  // AND_Gate and_56, 32 bits wide
  assign and_57_out = or_26_out & ~bit_extender_1_out;  // AND_Gate and_57, 32 bits wide
  assign and_58_out = or_27_out & ~bit_extender_1_out;  // AND_Gate and_58, 32 bits wide
  assign and_59_out = or_28_out & ~bit_extender_1_out;  // AND_Gate and_59, 32 bits wide
  assign and_60_out = or_29_out & ~bit_extender_1_out;  // AND_Gate and_60, 32 bits wide
  assign and_61_out = or_30_out & ~bit_extender_1_out;  // AND_Gate and_61, 32 bits wide
  assign and_62_out = or_31_out & ~bit_extender_1_out;  // AND_Gate and_62, 32 bits wide
  assign and_63_out = or_32_out & ~bit_extender_1_out;  // AND_Gate and_63, 32 bits wide
  assign and_64_out = or_33_out & ~bit_extender_1_out;  // AND_Gate and_64, 32 bits wide
  Register #(.width(32)) register_1 (.D(and_33_out), .en(or_1_out), .Q(out_6), .clk(clock), .clr(clear));
  Register #(.width(32)) register_2 (.D(and_34_out), .en(or_1_out), .Q(out_7), .clk(clock), .clr(clear));
  Register #(.width(32)) register_3 (.D(and_35_out), .en(or_1_out), .Q(out_8), .clk(clock), .clr(clear));
  Register #(.width(32)) register_4 (.D(and_36_out), .en(or_1_out), .Q(out_9), .clk(clock), .clr(clear));
  Register #(.width(32)) register_5 (.D(and_37_out), .en(or_1_out), .Q(out_10), .clk(clock), .clr(clear));
  Register #(.width(32)) register_6 (.D(and_38_out), .en(or_1_out), .Q(out_11), .clk(clock), .clr(clear));
  Register #(.width(32)) register_7 (.D(and_39_out), .en(or_1_out), .Q(out_12), .clk(clock), .clr(clear));
  Register #(.width(32)) register_8 (.D(and_40_out), .en(or_1_out), .Q(out_13), .clk(clock), .clr(clear));
  Register #(.width(32)) register_9 (.D(and_41_out), .en(or_1_out), .Q(out_14), .clk(clock), .clr(clear));
  Register #(.width(32)) register_10 (.D(and_42_out), .en(or_1_out), .Q(out_15), .clk(clock), .clr(clear));
  Register #(.width(32)) register_11 (.D(and_43_out), .en(or_1_out), .Q(out_16), .clk(clock), .clr(clear));
  Register #(.width(32)) register_12 (.D(and_44_out), .en(or_1_out), .Q(out_17), .clk(clock), .clr(clear));
  Register #(.width(32)) register_13 (.D(and_45_out), .en(or_1_out), .Q(out_18), .clk(clock), .clr(clear));
  Register #(.width(32)) register_14 (.D(and_46_out), .en(or_1_out), .Q(out_19), .clk(clock), .clr(clear));
  Register #(.width(32)) register_15 (.D(and_47_out), .en(or_1_out), .Q(out_20), .clk(clock), .clr(clear));
  Register #(.width(32)) register_16 (.D(and_48_out), .en(or_1_out), .Q(out_21), .clk(clock), .clr(clear));
  Register #(.width(32)) register_17 (.D(and_49_out), .en(or_1_out), .Q(out_22), .clk(clock), .clr(clear));
  Register #(.width(32)) register_18 (.D(and_50_out), .en(or_1_out), .Q(out_23), .clk(clock), .clr(clear));
  Register #(.width(32)) register_19 (.D(and_51_out), .en(or_1_out), .Q(out_24), .clk(clock), .clr(clear));
  Register #(.width(32)) register_20 (.D(and_52_out), .en(or_1_out), .Q(out_25), .clk(clock), .clr(clear));
  Register #(.width(32)) register_21 (.D(and_53_out), .en(or_1_out), .Q(out_26), .clk(clock), .clr(clear));
  Register #(.width(32)) register_22 (.D(and_54_out), .en(or_1_out), .Q(out_27), .clk(clock), .clr(clear));
  Register #(.width(32)) register_23 (.D(and_55_out), .en(or_1_out), .Q(out_28), .clk(clock), .clr(clear));
  Register #(.width(32)) register_24 (.D(and_56_out), .en(or_1_out), .Q(out_29), .clk(clock), .clr(clear));
  Register #(.width(32)) register_25 (.D(and_57_out), .en(or_1_out), .Q(out_30), .clk(clock), .clr(clear));
  Register #(.width(32)) register_26 (.D(and_58_out), .en(or_1_out), .Q(out_31), .clk(clock), .clr(clear));
  Register #(.width(32)) register_27 (.D(and_59_out), .en(or_1_out), .Q(out_32), .clk(clock), .clr(clear));
  Register #(.width(32)) register_28 (.D(and_60_out), .en(or_1_out), .Q(out_33), .clk(clock), .clr(clear));
  Register #(.width(32)) register_29 (.D(and_61_out), .en(or_1_out), .Q(out_34), .clk(clock), .clr(clear));
  Register #(.width(32)) register_30 (.D(and_62_out), .en(or_1_out), .Q(out_35), .clk(clock), .clr(clear));
  Register #(.width(32)) register_31 (.D(and_63_out), .en(or_1_out), .Q(out_36), .clk(clock), .clr(clear));
  Register #(.width(32)) register_32 (.D(and_64_out), .en(or_1_out), .Q(out_37), .clk(clock), .clr(clear));

  // Other names for the same wires on the sheet: CLR = clear
endmodule

module XYTOMATRIXSAVE (
  input  [4:0] X,
  input  [4:0] Y,
  input  write,
  input  clear,
  input  clock,
  output [31:0] out_6,
  output [31:0] out_7,
  output [31:0] out_8,
  output [31:0] out_9,
  output [31:0] out_10,
  output [31:0] out_11,
  output [31:0] out_12,
  output [31:0] out_13,
  output [31:0] out_14,
  output [31:0] out_15,
  output [31:0] out_16,
  output [31:0] out_17,
  output [31:0] out_18,
  output [31:0] out_19,
  output [31:0] out_20,
  output [31:0] out_21,
  output [31:0] out_22,
  output [31:0] out_23,
  output [31:0] out_24,
  output [31:0] out_25,
  output [31:0] out_26,
  output [31:0] out_27,
  output [31:0] out_28,
  output [31:0] out_29,
  output [31:0] out_30,
  output [31:0] out_31,
  output [31:0] out_32,
  output [31:0] out_33,
  output [31:0] out_34,
  output [31:0] out_35,
  output [31:0] out_36,
  output [31:0] out_37
);

  wire comparator_1_eq, comparator_2_eq, comparator_3_eq, comparator_4_eq, comparator_5_eq, comparator_6_eq,
       comparator_7_eq, comparator_8_eq, comparator_9_eq, comparator_10_eq, comparator_11_eq,
       comparator_12_eq, comparator_13_eq, comparator_14_eq, comparator_15_eq, comparator_16_eq,
       comparator_17_eq, comparator_18_eq, comparator_19_eq, comparator_20_eq, comparator_21_eq,
       comparator_22_eq, comparator_23_eq, comparator_24_eq, comparator_25_eq, comparator_26_eq,
       comparator_27_eq, comparator_28_eq, comparator_29_eq, comparator_30_eq, comparator_31_eq,
       comparator_32_eq, or_1_out;
  wire [31:0] and_1_out, and_2_out, and_3_out, and_4_out, and_5_out, and_6_out, and_7_out, and_8_out,
       and_9_out, and_10_out, and_11_out, and_12_out, and_13_out, and_14_out, and_15_out, and_16_out,
       and_17_out, and_18_out, and_19_out, and_20_out, and_21_out, and_22_out, and_23_out, and_24_out,
       and_25_out, and_26_out, and_27_out, and_28_out, and_29_out, and_30_out, and_31_out, and_32_out,
       and_33_out, and_34_out, and_35_out, and_36_out, and_37_out, and_38_out, and_39_out, and_40_out,
       and_41_out, and_42_out, and_43_out, and_44_out, and_45_out, and_46_out, and_47_out, and_48_out,
       and_49_out, and_50_out, and_51_out, and_52_out, and_53_out, and_54_out, and_55_out, and_56_out,
       and_57_out, and_58_out, and_59_out, and_60_out, and_61_out, and_62_out, and_63_out, and_64_out,
       bit_extender_1_out, bit_extender_2_out, bit_extender_3_out, bit_extender_4_out, bit_extender_5_out,
       bit_extender_6_out, bit_extender_7_out, bit_extender_8_out, bit_extender_9_out, bit_extender_10_out,
       bit_extender_11_out, bit_extender_12_out, bit_extender_13_out, bit_extender_14_out,
       bit_extender_15_out, bit_extender_16_out, bit_extender_17_out, bit_extender_18_out,
       bit_extender_19_out, bit_extender_20_out, bit_extender_21_out, bit_extender_22_out,
       bit_extender_23_out, bit_extender_24_out, bit_extender_25_out, bit_extender_26_out,
       bit_extender_27_out, bit_extender_28_out, bit_extender_29_out, bit_extender_30_out,
       bit_extender_31_out, bit_extender_32_out, bit_extender_33_out, or_2_out, or_3_out, or_4_out, or_5_out,
       or_6_out, or_7_out, or_8_out, or_9_out, or_10_out, or_11_out, or_12_out, or_13_out, or_14_out,
       or_15_out, or_16_out, or_17_out, or_18_out, or_19_out, or_20_out, or_21_out, or_22_out, or_23_out,
       or_24_out, or_25_out, or_26_out, or_27_out, or_28_out, or_29_out, or_30_out, or_31_out, or_32_out,
       or_33_out, shifter_1_out;

  assign bit_extender_1_out = {{31{clear}}, clear};  // Bit_Extender bit_extender_1
  Shifter #(.width(32)) shifter_1 (.in(32'h1), .\dist (Y), .out(shifter_1_out));
  or or_1 (or_1_out, write, clear);
  Comparator #(.width(5)) comparator_1 (.a({5{1'b0}}), .b(X), .eq(comparator_1_eq));  // open: gt, lt
  assign bit_extender_2_out = {{31{comparator_1_eq}}, comparator_1_eq};  // Bit_Extender bit_extender_2
  assign bit_extender_3_out = {{31{comparator_2_eq}}, comparator_2_eq};  // Bit_Extender bit_extender_3
  Comparator #(.width(5)) comparator_2 (.a(5'b00001), .b(X), .eq(comparator_2_eq));  // open: gt, lt
  assign bit_extender_4_out = {{31{comparator_3_eq}}, comparator_3_eq};  // Bit_Extender bit_extender_4
  Comparator #(.width(5)) comparator_3 (.a(5'b00010), .b(X), .eq(comparator_3_eq));  // open: gt, lt
  assign bit_extender_5_out = {{31{comparator_4_eq}}, comparator_4_eq};  // Bit_Extender bit_extender_5
  Comparator #(.width(5)) comparator_4 (.a(5'b00011), .b(X), .eq(comparator_4_eq));  // open: gt, lt
  Comparator #(.width(5)) comparator_5 (.a(5'b00100), .b(X), .eq(comparator_5_eq));  // open: gt, lt
  assign bit_extender_6_out = {{31{comparator_5_eq}}, comparator_5_eq};  // Bit_Extender bit_extender_6
  Comparator #(.width(5)) comparator_6 (.a(5'b00101), .b(X), .eq(comparator_6_eq));  // open: gt, lt
  assign bit_extender_7_out = {{31{comparator_6_eq}}, comparator_6_eq};  // Bit_Extender bit_extender_7
  assign bit_extender_8_out = {{31{comparator_7_eq}}, comparator_7_eq};  // Bit_Extender bit_extender_8
  Comparator #(.width(5)) comparator_7 (.a(5'b00110), .b(X), .eq(comparator_7_eq));  // open: gt, lt
  assign bit_extender_9_out = {{31{comparator_8_eq}}, comparator_8_eq};  // Bit_Extender bit_extender_9
  Comparator #(.width(5)) comparator_8 (.a(5'b00111), .b(X), .eq(comparator_8_eq));  // open: gt, lt
  assign bit_extender_10_out = {{31{comparator_9_eq}}, comparator_9_eq};  // Bit_Extender bit_extender_10
  Comparator #(.width(5)) comparator_9 (.a(5'b01000), .b(X), .eq(comparator_9_eq));  // open: gt, lt
  assign bit_extender_11_out = {{31{comparator_10_eq}}, comparator_10_eq};  // Bit_Extender bit_extender_11
  Comparator #(.width(5)) comparator_10 (.a(5'b01001), .b(X), .eq(comparator_10_eq));  // open: gt, lt
  assign bit_extender_12_out = {{31{comparator_11_eq}}, comparator_11_eq};  // Bit_Extender bit_extender_12
  Comparator #(.width(5)) comparator_11 (.a(5'b01010), .b(X), .eq(comparator_11_eq));  // open: gt, lt
  assign bit_extender_13_out = {{31{comparator_12_eq}}, comparator_12_eq};  // Bit_Extender bit_extender_13
  Comparator #(.width(5)) comparator_12 (.a(5'b01011), .b(X), .eq(comparator_12_eq));  // open: gt, lt
  assign bit_extender_14_out = {{31{comparator_13_eq}}, comparator_13_eq};  // Bit_Extender bit_extender_14
  Comparator #(.width(5)) comparator_13 (.a(5'b01100), .b(X), .eq(comparator_13_eq));  // open: gt, lt
  assign bit_extender_15_out = {{31{comparator_14_eq}}, comparator_14_eq};  // Bit_Extender bit_extender_15
  Comparator #(.width(5)) comparator_14 (.a(5'b01101), .b(X), .eq(comparator_14_eq));  // open: gt, lt
  Comparator #(.width(5)) comparator_15 (.a(5'b01110), .b(X), .eq(comparator_15_eq));  // open: gt, lt
  assign bit_extender_16_out = {{31{comparator_15_eq}}, comparator_15_eq};  // Bit_Extender bit_extender_16
  Comparator #(.width(5)) comparator_16 (.a(5'b01111), .b(X), .eq(comparator_16_eq));  // open: gt, lt
  assign bit_extender_17_out = {{31{comparator_16_eq}}, comparator_16_eq};  // Bit_Extender bit_extender_17
  assign bit_extender_18_out = {{31{comparator_17_eq}}, comparator_17_eq};  // Bit_Extender bit_extender_18
  Comparator #(.width(5)) comparator_17 (.a(5'b10000), .b(X), .eq(comparator_17_eq));  // open: gt, lt
  Comparator #(.width(5)) comparator_18 (.a(5'b10001), .b(X), .eq(comparator_18_eq));  // open: gt, lt
  assign bit_extender_19_out = {{31{comparator_18_eq}}, comparator_18_eq};  // Bit_Extender bit_extender_19
  assign bit_extender_20_out = {{31{comparator_19_eq}}, comparator_19_eq};  // Bit_Extender bit_extender_20
  Comparator #(.width(5)) comparator_19 (.a(5'b10010), .b(X), .eq(comparator_19_eq));  // open: gt, lt
  Comparator #(.width(5)) comparator_20 (.a(5'b10011), .b(X), .eq(comparator_20_eq));  // open: gt, lt
  assign bit_extender_21_out = {{31{comparator_20_eq}}, comparator_20_eq};  // Bit_Extender bit_extender_21
  assign bit_extender_22_out = {{31{comparator_21_eq}}, comparator_21_eq};  // Bit_Extender bit_extender_22
  Comparator #(.width(5)) comparator_21 (.a(5'b10100), .b(X), .eq(comparator_21_eq));  // open: gt, lt
  Comparator #(.width(5)) comparator_22 (.a(5'b10101), .b(X), .eq(comparator_22_eq));  // open: gt, lt
  assign bit_extender_23_out = {{31{comparator_22_eq}}, comparator_22_eq};  // Bit_Extender bit_extender_23
  assign bit_extender_24_out = {{31{comparator_23_eq}}, comparator_23_eq};  // Bit_Extender bit_extender_24
  Comparator #(.width(5)) comparator_23 (.a(5'b10110), .b(X), .eq(comparator_23_eq));  // open: gt, lt
  assign bit_extender_25_out = {{31{comparator_24_eq}}, comparator_24_eq};  // Bit_Extender bit_extender_25
  Comparator #(.width(5)) comparator_24 (.a(5'b10111), .b(X), .eq(comparator_24_eq));  // open: gt, lt
  Comparator #(.width(5)) comparator_25 (.a(5'b11000), .b(X), .eq(comparator_25_eq));  // open: gt, lt
  assign bit_extender_26_out = {{31{comparator_25_eq}}, comparator_25_eq};  // Bit_Extender bit_extender_26
  assign bit_extender_27_out = {{31{comparator_26_eq}}, comparator_26_eq};  // Bit_Extender bit_extender_27
  Comparator #(.width(5)) comparator_26 (.a(5'b11001), .b(X), .eq(comparator_26_eq));  // open: gt, lt
  Comparator #(.width(5)) comparator_27 (.a(5'b11010), .b(X), .eq(comparator_27_eq));  // open: gt, lt
  assign bit_extender_28_out = {{31{comparator_27_eq}}, comparator_27_eq};  // Bit_Extender bit_extender_28
  Comparator #(.width(5)) comparator_28 (.a(5'b11011), .b(X), .eq(comparator_28_eq));  // open: gt, lt
  assign bit_extender_29_out = {{31{comparator_28_eq}}, comparator_28_eq};  // Bit_Extender bit_extender_29
  Comparator #(.width(5)) comparator_29 (.a(5'b11100), .b(X), .eq(comparator_29_eq));  // open: gt, lt
  assign bit_extender_30_out = {{31{comparator_29_eq}}, comparator_29_eq};  // Bit_Extender bit_extender_30
  assign bit_extender_31_out = {{31{comparator_30_eq}}, comparator_30_eq};  // Bit_Extender bit_extender_31
  Comparator #(.width(5)) comparator_30 (.a(5'b11101), .b(X), .eq(comparator_30_eq));  // open: gt, lt
  Comparator #(.width(5)) comparator_31 (.a(5'b11110), .b(X), .eq(comparator_31_eq));  // open: gt, lt
  assign bit_extender_32_out = {{31{comparator_31_eq}}, comparator_31_eq};  // Bit_Extender bit_extender_32
  Comparator #(.width(5)) comparator_32 (.a({5{1'b1}}), .b(X), .eq(comparator_32_eq));  // open: gt, lt
  assign bit_extender_33_out = {{31{comparator_32_eq}}, comparator_32_eq};  // Bit_Extender bit_extender_33
  assign and_1_out = bit_extender_2_out & shifter_1_out;  // AND_Gate and_1, 32 bits wide
  assign or_2_out = and_1_out | out_6;  // OR_Gate or_2, 32 bits wide
  assign and_2_out = bit_extender_3_out & shifter_1_out;  // AND_Gate and_2, 32 bits wide
  assign or_3_out = and_2_out | out_7;  // OR_Gate or_3, 32 bits wide
  assign and_3_out = bit_extender_4_out & shifter_1_out;  // AND_Gate and_3, 32 bits wide
  assign or_4_out = and_3_out | out_8;  // OR_Gate or_4, 32 bits wide
  assign and_4_out = bit_extender_5_out & shifter_1_out;  // AND_Gate and_4, 32 bits wide
  assign or_5_out = and_4_out | out_9;  // OR_Gate or_5, 32 bits wide
  assign and_5_out = bit_extender_6_out & shifter_1_out;  // AND_Gate and_5, 32 bits wide
  assign or_6_out = and_5_out | out_10;  // OR_Gate or_6, 32 bits wide
  assign and_6_out = bit_extender_7_out & shifter_1_out;  // AND_Gate and_6, 32 bits wide
  assign or_7_out = and_6_out | out_11;  // OR_Gate or_7, 32 bits wide
  assign and_7_out = bit_extender_8_out & shifter_1_out;  // AND_Gate and_7, 32 bits wide
  assign or_8_out = and_7_out | out_12;  // OR_Gate or_8, 32 bits wide
  assign and_8_out = bit_extender_9_out & shifter_1_out;  // AND_Gate and_8, 32 bits wide
  assign or_9_out = and_8_out | out_13;  // OR_Gate or_9, 32 bits wide
  assign and_9_out = bit_extender_10_out & shifter_1_out;  // AND_Gate and_9, 32 bits wide
  assign or_10_out = and_9_out | out_14;  // OR_Gate or_10, 32 bits wide
  assign and_10_out = bit_extender_11_out & shifter_1_out;  // AND_Gate and_10, 32 bits wide
  assign or_11_out = and_10_out | out_15;  // OR_Gate or_11, 32 bits wide
  assign and_11_out = bit_extender_12_out & shifter_1_out;  // AND_Gate and_11, 32 bits wide
  assign or_12_out = and_11_out | out_16;  // OR_Gate or_12, 32 bits wide
  assign and_12_out = bit_extender_13_out & shifter_1_out;  // AND_Gate and_12, 32 bits wide
  assign or_13_out = and_12_out | out_17;  // OR_Gate or_13, 32 bits wide
  assign and_13_out = bit_extender_14_out & shifter_1_out;  // AND_Gate and_13, 32 bits wide
  assign or_14_out = and_13_out | out_18;  // OR_Gate or_14, 32 bits wide
  assign and_14_out = bit_extender_15_out & shifter_1_out;  // AND_Gate and_14, 32 bits wide
  assign or_15_out = and_14_out | out_19;  // OR_Gate or_15, 32 bits wide
  assign and_15_out = bit_extender_16_out & shifter_1_out;  // AND_Gate and_15, 32 bits wide
  assign or_16_out = and_15_out | out_20;  // OR_Gate or_16, 32 bits wide
  assign and_16_out = bit_extender_17_out & shifter_1_out;  // AND_Gate and_16, 32 bits wide
  assign or_17_out = and_16_out | out_21;  // OR_Gate or_17, 32 bits wide
  assign and_17_out = bit_extender_18_out & shifter_1_out;  // AND_Gate and_17, 32 bits wide
  assign or_18_out = and_17_out | out_22;  // OR_Gate or_18, 32 bits wide
  assign and_18_out = bit_extender_19_out & shifter_1_out;  // AND_Gate and_18, 32 bits wide
  assign or_19_out = and_18_out | out_23;  // OR_Gate or_19, 32 bits wide
  assign and_19_out = bit_extender_20_out & shifter_1_out;  // AND_Gate and_19, 32 bits wide
  assign or_20_out = and_19_out | out_24;  // OR_Gate or_20, 32 bits wide
  assign and_20_out = bit_extender_21_out & shifter_1_out;  // AND_Gate and_20, 32 bits wide
  assign or_21_out = and_20_out | out_25;  // OR_Gate or_21, 32 bits wide
  assign and_21_out = bit_extender_22_out & shifter_1_out;  // AND_Gate and_21, 32 bits wide
  assign or_22_out = and_21_out | out_26;  // OR_Gate or_22, 32 bits wide
  assign and_22_out = bit_extender_23_out & shifter_1_out;  // AND_Gate and_22, 32 bits wide
  assign or_23_out = and_22_out | out_27;  // OR_Gate or_23, 32 bits wide
  assign and_23_out = bit_extender_24_out & shifter_1_out;  // AND_Gate and_23, 32 bits wide
  assign or_24_out = and_23_out | out_28;  // OR_Gate or_24, 32 bits wide
  assign and_24_out = bit_extender_25_out & shifter_1_out;  // AND_Gate and_24, 32 bits wide
  assign or_25_out = and_24_out | out_29;  // OR_Gate or_25, 32 bits wide
  assign and_25_out = bit_extender_26_out & shifter_1_out;  // AND_Gate and_25, 32 bits wide
  assign or_26_out = and_25_out | out_30;  // OR_Gate or_26, 32 bits wide
  assign and_26_out = bit_extender_27_out & shifter_1_out;  // AND_Gate and_26, 32 bits wide
  assign or_27_out = and_26_out | out_31;  // OR_Gate or_27, 32 bits wide
  assign and_27_out = bit_extender_28_out & shifter_1_out;  // AND_Gate and_27, 32 bits wide
  assign or_28_out = and_27_out | out_32;  // OR_Gate or_28, 32 bits wide
  assign and_28_out = bit_extender_29_out & shifter_1_out;  // AND_Gate and_28, 32 bits wide
  assign or_29_out = and_28_out | out_33;  // OR_Gate or_29, 32 bits wide
  assign and_29_out = bit_extender_30_out & shifter_1_out;  // AND_Gate and_29, 32 bits wide
  assign or_30_out = and_29_out | out_34;  // OR_Gate or_30, 32 bits wide
  assign and_30_out = bit_extender_31_out & shifter_1_out;  // AND_Gate and_30, 32 bits wide
  assign or_31_out = and_30_out | out_35;  // OR_Gate or_31, 32 bits wide
  assign and_31_out = bit_extender_32_out & shifter_1_out;  // AND_Gate and_31, 32 bits wide
  assign or_32_out = and_31_out | out_36;  // OR_Gate or_32, 32 bits wide
  assign and_32_out = bit_extender_33_out & shifter_1_out;  // AND_Gate and_32, 32 bits wide
  assign or_33_out = and_32_out | out_37;  // OR_Gate or_33, 32 bits wide
  assign and_33_out = or_2_out & ~bit_extender_1_out;  // AND_Gate and_33, 32 bits wide
  assign and_34_out = or_3_out & ~bit_extender_1_out;  // AND_Gate and_34, 32 bits wide
  assign and_35_out = or_4_out & ~bit_extender_1_out;  // AND_Gate and_35, 32 bits wide
  assign and_36_out = or_5_out & ~bit_extender_1_out;  // AND_Gate and_36, 32 bits wide
  assign and_37_out = or_6_out & ~bit_extender_1_out;  // AND_Gate and_37, 32 bits wide
  assign and_38_out = or_7_out & ~bit_extender_1_out;  // AND_Gate and_38, 32 bits wide
  assign and_39_out = or_8_out & ~bit_extender_1_out;  // AND_Gate and_39, 32 bits wide
  assign and_40_out = or_9_out & ~bit_extender_1_out;  // AND_Gate and_40, 32 bits wide
  assign and_41_out = or_10_out & ~bit_extender_1_out;  // AND_Gate and_41, 32 bits wide
  assign and_42_out = or_11_out & ~bit_extender_1_out;  // AND_Gate and_42, 32 bits wide
  assign and_43_out = or_12_out & ~bit_extender_1_out;  // AND_Gate and_43, 32 bits wide
  assign and_44_out = or_13_out & ~bit_extender_1_out;  // AND_Gate and_44, 32 bits wide
  assign and_45_out = or_14_out & ~bit_extender_1_out;  // AND_Gate and_45, 32 bits wide
  assign and_46_out = or_15_out & ~bit_extender_1_out;  // AND_Gate and_46, 32 bits wide
  assign and_47_out = or_16_out & ~bit_extender_1_out;  // AND_Gate and_47, 32 bits wide
  assign and_48_out = or_17_out & ~bit_extender_1_out;  // AND_Gate and_48, 32 bits wide
  assign and_49_out = or_18_out & ~bit_extender_1_out;  // AND_Gate and_49, 32 bits wide
  assign and_50_out = or_19_out & ~bit_extender_1_out;  // AND_Gate and_50, 32 bits wide
  assign and_51_out = or_20_out & ~bit_extender_1_out;  // AND_Gate and_51, 32 bits wide
  assign and_52_out = or_21_out & ~bit_extender_1_out;  // AND_Gate and_52, 32 bits wide
  assign and_53_out = or_22_out & ~bit_extender_1_out;  // AND_Gate and_53, 32 bits wide
  assign and_54_out = or_23_out & ~bit_extender_1_out;  // AND_Gate and_54, 32 bits wide
  assign and_55_out = or_24_out & ~bit_extender_1_out;  // AND_Gate and_55, 32 bits wide
  assign and_56_out = or_25_out & ~bit_extender_1_out;  // AND_Gate and_56, 32 bits wide
  assign and_57_out = or_26_out & ~bit_extender_1_out;  // AND_Gate and_57, 32 bits wide
  assign and_58_out = or_27_out & ~bit_extender_1_out;  // AND_Gate and_58, 32 bits wide
  assign and_59_out = or_28_out & ~bit_extender_1_out;  // AND_Gate and_59, 32 bits wide
  assign and_60_out = or_29_out & ~bit_extender_1_out;  // AND_Gate and_60, 32 bits wide
  assign and_61_out = or_30_out & ~bit_extender_1_out;  // AND_Gate and_61, 32 bits wide
  assign and_62_out = or_31_out & ~bit_extender_1_out;  // AND_Gate and_62, 32 bits wide
  assign and_63_out = or_32_out & ~bit_extender_1_out;  // AND_Gate and_63, 32 bits wide
  assign and_64_out = or_33_out & ~bit_extender_1_out;  // AND_Gate and_64, 32 bits wide
  Register #(.width(32)) register_1 (.D(and_33_out), .en(or_1_out), .Q(out_6), .clk(clock));  // open: clr
  Register #(.width(32)) register_2 (.D(and_34_out), .en(or_1_out), .Q(out_7), .clk(clock));  // open: clr
  Register #(.width(32)) register_3 (.D(and_35_out), .en(or_1_out), .Q(out_8), .clk(clock));  // open: clr
  Register #(.width(32)) register_4 (.D(and_36_out), .en(or_1_out), .Q(out_9), .clk(clock));  // open: clr
  Register #(.width(32)) register_5 (.D(and_37_out), .en(or_1_out), .Q(out_10), .clk(clock));  // open: clr
  Register #(.width(32)) register_6 (.D(and_38_out), .en(or_1_out), .Q(out_11), .clk(clock));  // open: clr
  Register #(.width(32)) register_7 (.D(and_39_out), .en(or_1_out), .Q(out_12), .clk(clock));  // open: clr
  Register #(.width(32)) register_8 (.D(and_40_out), .en(or_1_out), .Q(out_13), .clk(clock));  // open: clr
  Register #(.width(32)) register_9 (.D(and_41_out), .en(or_1_out), .Q(out_14), .clk(clock));  // open: clr
  Register #(.width(32)) register_10 (.D(and_42_out), .en(or_1_out), .Q(out_15), .clk(clock));  // open: clr
  Register #(.width(32)) register_11 (.D(and_43_out), .en(or_1_out), .Q(out_16), .clk(clock));  // open: clr
  Register #(.width(32)) register_12 (.D(and_44_out), .en(or_1_out), .Q(out_17), .clk(clock));  // open: clr
  Register #(.width(32)) register_13 (.D(and_45_out), .en(or_1_out), .Q(out_18), .clk(clock));  // open: clr
  Register #(.width(32)) register_14 (.D(and_46_out), .en(or_1_out), .Q(out_19), .clk(clock));  // open: clr
  Register #(.width(32)) register_15 (.D(and_47_out), .en(or_1_out), .Q(out_20), .clk(clock));  // open: clr
  Register #(.width(32)) register_16 (.D(and_48_out), .en(or_1_out), .Q(out_21), .clk(clock));  // open: clr
  Register #(.width(32)) register_17 (.D(and_49_out), .en(or_1_out), .Q(out_22), .clk(clock));  // open: clr
  Register #(.width(32)) register_18 (.D(and_50_out), .en(or_1_out), .Q(out_23), .clk(clock));  // open: clr
  Register #(.width(32)) register_19 (.D(and_51_out), .en(or_1_out), .Q(out_24), .clk(clock));  // open: clr
  Register #(.width(32)) register_20 (.D(and_52_out), .en(or_1_out), .Q(out_25), .clk(clock));  // open: clr
  Register #(.width(32)) register_21 (.D(and_53_out), .en(or_1_out), .Q(out_26), .clk(clock));  // open: clr
  Register #(.width(32)) register_22 (.D(and_54_out), .en(or_1_out), .Q(out_27), .clk(clock));  // open: clr
  Register #(.width(32)) register_23 (.D(and_55_out), .en(or_1_out), .Q(out_28), .clk(clock));  // open: clr
  Register #(.width(32)) register_24 (.D(and_56_out), .en(or_1_out), .Q(out_29), .clk(clock));  // open: clr
  Register #(.width(32)) register_25 (.D(and_57_out), .en(or_1_out), .Q(out_30), .clk(clock));  // open: clr
  Register #(.width(32)) register_26 (.D(and_58_out), .en(or_1_out), .Q(out_31), .clk(clock));  // open: clr
  Register #(.width(32)) register_27 (.D(and_59_out), .en(or_1_out), .Q(out_32), .clk(clock));  // open: clr
  Register #(.width(32)) register_28 (.D(and_60_out), .en(or_1_out), .Q(out_33), .clk(clock));  // open: clr
  Register #(.width(32)) register_29 (.D(and_61_out), .en(or_1_out), .Q(out_34), .clk(clock));  // open: clr
  Register #(.width(32)) register_30 (.D(and_62_out), .en(or_1_out), .Q(out_35), .clk(clock));  // open: clr
  Register #(.width(32)) register_31 (.D(and_63_out), .en(or_1_out), .Q(out_36), .clk(clock));  // open: clr
  Register #(.width(32)) register_32 (.D(and_64_out), .en(or_1_out), .Q(out_37), .clk(clock));  // open: clr
endmodule
