// Logisim project AnotherCpuWOOOORKS.circ as structural Verilog: 3 circuits, main circuit main
module main (
  input  in_1
);

  wire ADD, alu_1_equal, alu_1_greater_than, alu_1_less_than, and_2_out, and_3_out, and_4_out, and_5_out,
       and_6_out, Clk, clock_1_out, CMP, CPR, DWP, EQ, GT, HLT, JGT, JIE, JLT, JMP, LDM, LDR, LT, MCL, NAND,
       NOP, not_1_out, not_2_out, not_3_out, not_4_out, not_5_out, or_1_out, or_2_out, or_3_out, or_4_out,
       or_5_out, or_6_out, R, RCL, SMV, SPC, SRV, SUB;
  wire [3:0] controlled_buffer_10_out, RegA;
  wire [5:0] rgb_video_1_p8, rgb_video_1_p9;
  wire [7:0] bit_extender_3_out, bit_extender_4_out, controlled_buffer_1_out, counter_1_q, not_6_out;
  wire [11:0] Int12;
  wire [15:0] alu_1_output, bit_extender_1_out, bit_extender_2_out, controlled_buffer_2_out,
       controlled_buffer_5_out, RegAOut, RegBOut, register_2_q, Secondary_RAM_For_Values_dout;
  wire [20:0] ram_1_dout;
  wire [20:16] register_1_q;

  Clock clock_1 (.out(clock_1_out));
  Button Reboot (.out(R));
  Decoder #(.enable("false"), .select(5)) decoder_1 (
    .out0(NOP), .out1(ADD), .out2(SUB), .out3(NAND), .out4(CMP), .out5(JMP), .out6(JGT), .out7(JIE),
    .out8(JLT), .out9(SRV), .out10(CPR), .out11(RCL), .out12(MCL), .out13(LDM), .out14(LDR), .out15(SMV),
    .out16(SPC), .out17(DWP), .out18(HLT), .sel(register_1_q));  // open: out19, out20, out21, out22, out23, out24, out25, out26, out27, out28, out29, out30, out31
  and and_1 (Clk, clock_1_out, ~HLT);  // AND_Gate
  and and_2 (and_2_out, JGT, GT);
  or or_1 (or_1_out, JMP, and_2_out, and_3_out, and_4_out);
  and and_3 (and_3_out, JIE, EQ);
  and and_4 (and_4_out, JLT, LT);
  assign controlled_buffer_1_out = or_1_out ? Int12[7:0] : 8'bz;  // Controlled_Buffer controlled_buffer_1
  not not_1 (not_1_out, or_1_out);
  Counter counter_1 (
    .load(or_1_out), .D(controlled_buffer_1_out), .count(not_1_out), .Q(counter_1_q), .clk(Clk), .clr(R));  // open: carry, up
  not not_2 (not_2_out, Clk);
  not not_3 (not_3_out, not_2_out);
  assign bit_extender_1_out = {{4{Int12[11]}}, Int12};  // Bit_Extender bit_extender_1
  RAM #(.asyncread("true"), .dataWidth(21), .\type ("nonvolatile")) ram_1 (
    .addr(counter_1_q), .clk(and_5_out), .dout(ram_1_dout));  // open: we, oe, din
  not not_4 (not_4_out, not_3_out);
  and and_5 (and_5_out, not_4_out, Clk);
  RAM #(.addrWidth(4), .asyncread("true"), .dataWidth(16), .\type ("nonvolatile")) Secondary_RAM_For_Values (
    .addr(RegA), .we(or_2_out), .clk(Clk), .din(controlled_buffer_2_out), .dout(Secondary_RAM_For_Values_dout));  // open: oe
  or or_2 (or_2_out, MCL, SMV, LDR);
  assign controlled_buffer_2_out = LDR ? RegBOut : 16'bz;  // Controlled_Buffer controlled_buffer_2
  assign controlled_buffer_2_out = SMV ? bit_extender_1_out : 16'bz;  // Controlled_Buffer controlled_buffer_3
  assign controlled_buffer_2_out = MCL ? {16{1'b0}} : 16'bz;  // Controlled_Buffer controlled_buffer_4
  Pull_Resistor pull_resistor_1 (.node(Int12));
  buf or_3 (or_3_out, SRV);  // OR_Gate
  or or_4 (or_4_out, ADD, SUB, NAND);
  assign bit_extender_2_out = {{4{Int12[11]}}, Int12};  // Bit_Extender bit_extender_2
  assign controlled_buffer_5_out = or_3_out ? bit_extender_2_out : 16'bz;  // Controlled_Buffer controlled_buffer_5
  assign controlled_buffer_5_out = CPR ? RegBOut : 16'bz;  // Controlled_Buffer controlled_buffer_6
  assign controlled_buffer_5_out = or_4_out ? alu_1_output : 16'bz;  // Controlled_Buffer controlled_buffer_7
  assign controlled_buffer_5_out = RCL ? {16{1'b0}} : 16'bz;  // Controlled_Buffer controlled_buffer_8
  assign controlled_buffer_5_out = LDM ? Secondary_RAM_For_Values_dout : 16'bz;  // Controlled_Buffer controlled_buffer_9
  not not_5 (not_5_out, LDM);
  assign controlled_buffer_10_out = not_5_out ? RegA : 4'bz;  // Controlled_Buffer controlled_buffer_10
  assign controlled_buffer_10_out = LDM ? Int12[11:8] : 4'bz;  // Controlled_Buffer controlled_buffer_11
  RegisterBank registerbank_1 (
    .AOutput(RegAOut), .BOutput(RegBOut), .Write(or_5_out), .InData(controlled_buffer_5_out), .Clock(Clk),
    .Select(controlled_buffer_10_out), .ASelect(RegA), .BSelect(Int12[11:8]));  // open: MasterReset
  or or_5 (or_5_out, CPR, LDM, or_4_out, SRV, RCL);
  Register #(.trigger("high"), .width(21)) register_1 (
    .D(ram_1_dout), .Q({register_1_q, RegA, Int12}), .clk(or_6_out));  // open: en, clr
  or or_6 (or_6_out, R, Clk);
  ALU alu_1 (
    .A(RegAOut), .B(RegBOut), .OpCode(register_1_q), .Output(alu_1_output),
    .Greater_Than(alu_1_greater_than), .Equal(alu_1_equal), .Less_Than(alu_1_less_than));  // open: Carry_Borrow, C_Out, B_Out, Negative, Overflow, Zero
  D_Flip_Flop #(.trigger("high")) d_ff_1 (.clk(CMP), .D(CMP), .Q(GT), .Qn(EQ));  // open: preset, reset
  D_Flip_Flop #(.trigger("high")) d_ff_2 (.clk(CMP), .D(CMP), .Q(EQ), .Qn(LT));  // open: preset, reset
  D_Flip_Flop #(.trigger("high")) d_ff_3 (.clk(CMP), .D(alu_1_less_than), .Q(LT));  // open: Qn, preset, reset
  Register #(.width(16)) register_2 (.D({RegA, Int12}), .en(and_6_out), .Q(register_2_q), .clk(and_6_out), .clr(R));
  and and_6 (and_6_out, SPC, ~R);  // AND_Gate
  // RGB_Video #(.cursor("No Cursor"), .height(64), .scale(8), .width(64)) rgb_video_1: pin names not known; wires that end beside it: CMP, alu_1_greater_than, CMP, alu_1_equal, R, Clk, DWP, rgb_video_1_p8, rgb_video_1_p9, register_2_q
  assign not_6_out = ~bit_extender_4_out;  // NOT_Gate not_6, 8 bits wide
  Bit_Extender #(.in_width(16), .out_width(8)) bit_extender_3 (.in(RegAOut), .out(bit_extender_3_out));
  Bit_Extender #(.in_width(16), .out_width(8)) bit_extender_4 (.in(RegBOut), .out(bit_extender_4_out));
  Bit_Extender #(.out_width(6)) bit_extender_5 (.in(not_6_out), .out(rgb_video_1_p9));
  Bit_Extender #(.out_width(6)) bit_extender_6 (.in(bit_extender_3_out), .out(rgb_video_1_p8));

  // Other names for the same wires on the sheet: MAdr[7:0] = Int12[7:0]; RegB[3:0] = Int12[11:8]

  // Notes on the sheet:
  //   The fix is by making the IR update on rise
  //   MCL and LDR dont work because the counter cant be updated on high otherwise it gives errors
  //   TODO: FIX THE STUPID MCL LDM AND LDR(LDR IS REALLY USEFUL AND NEEDED FOR BRESENHAM DRAWiNG)
endmodule

module ALU (
  input  [15:0] A,
  input  [15:0] B,
  input  [4:0] OpCode,
  input  Carry_Borrow,
  output C_Out,
  output B_Out,
  output [15:0] Output,
  output Negative,
  output Overflow,
  output Zero,
  output Greater_Than,
  output Equal,
  output Less_Than
);

  wire and_2_out, comparator_1_eq, comparator_1_gt, comparator_1_lt, nor_1_out;
  wire [2:0] controlled_buffer_1_out;
  wire [15:0] adder_1_out, nand_1_out, subtractor_1_out;

  Pull_Resistor pull_resistor_1 (.node(A));
  Pull_Resistor pull_resistor_2 (.node(B));
  Pull_Resistor pull_resistor_3 (.node(Carry_Borrow));
  assign controlled_buffer_1_out = nor_1_out ? OpCode[2:0] : 3'bz;  // Controlled_Buffer controlled_buffer_1
  nor nor_1 (nor_1_out, OpCode[3], OpCode[4]);
  Adder #(.width(16)) adder_1 (.a(A), .b(B), .out(adder_1_out), .cin(Carry_Borrow), .cout(C_Out));
  Subtractor #(.width(16)) subtractor_1 (.a(A), .b(B), .out(subtractor_1_out), .bin(Carry_Borrow), .bout(B_Out));
  assign nand_1_out = ~(A & B);  // NAND_Gate nand_1, 16 bits wide
  Multiplexer #(.select(3), .width(16)) multiplexer_1 (
    .in0({16{1'b0}}), .in1(adder_1_out), .in2(subtractor_1_out), .in3(nand_1_out), .in4({16{1'b0}}),
    .in5({16{1'b0}}), .in6({16{1'b0}}), .in7({16{1'b0}}), .out({Negative, Output[14:0]}),
    .sel(controlled_buffer_1_out));
  Pull_Resistor #(.pull(1)) pull_resistor_4 (.node(controlled_buffer_1_out[0]));
  Pull_Resistor #(.pull(1)) pull_resistor_5 (.node(controlled_buffer_1_out[1]));
  Pull_Resistor #(.pull(1)) pull_resistor_6 (.node(controlled_buffer_1_out[2]));
  Comparator #(.width(16)) comparator_1 (
    .a(A), .b(B), .gt(comparator_1_gt), .eq(comparator_1_eq), .lt(comparator_1_lt));
  and and_1 (Overflow, C_Out, controlled_buffer_1_out[0], ~controlled_buffer_1_out[1], ~controlled_buffer_1_out[2]);  // AND_Gate
  and and_2 (and_2_out, ~controlled_buffer_1_out[0], ~controlled_buffer_1_out[1], controlled_buffer_1_out[2]);  // AND_Gate
  Pull_Resistor pull_resistor_7 (.node(Greater_Than));
  assign Greater_Than = and_2_out ? comparator_1_gt : 1'bz;  // Controlled_Buffer controlled_buffer_2
  Pull_Resistor pull_resistor_8 (.node(Equal));
  assign Equal = and_2_out ? comparator_1_eq : 1'bz;  // Controlled_Buffer controlled_buffer_3
  assign Less_Than = and_2_out ? comparator_1_lt : 1'bz;  // Controlled_Buffer controlled_buffer_4
  nor nor_2 (Zero, Output[0], Output[1], Output[2], Output[3], Output[4], Output[5], Output[6], Output[7], Output[8], Output[9], Output[10], Output[11], Output[12], Output[13], Output[14], Negative, Overflow);
  Pull_Resistor pull_resistor_9 (.node(Less_Than));

  assign Output[15] = Negative;

  // Other names for the same wires on the sheet: Bout = B_Out; Cout = C_Out; Ovrf = Overflow

  // Notes on the sheet:
  //   Flags
endmodule

module RegisterBank (
  input  Write,
  input  [3:0] Select,
  input  [15:0] InData,
  input  Clock,
  input  MasterReset,
  input  [3:0] ASelect,
  input  [3:0] BSelect,
  output [15:0] AOutput,
  output [15:0] BOutput
);

  wire demultiplexer_1_out0, demultiplexer_1_out1, demultiplexer_1_out2, demultiplexer_1_out3,
       demultiplexer_1_out4, demultiplexer_1_out5, demultiplexer_1_out6, demultiplexer_1_out7,
       demultiplexer_1_out8, demultiplexer_1_out9, demultiplexer_1_out10, demultiplexer_1_out11,
       demultiplexer_1_out12, demultiplexer_1_out13, demultiplexer_1_out14, demultiplexer_1_out15;
  wire [15:0] Reg0_q, Reg1_q, Reg2_q, Reg3_q, Reg4_q, Reg5_q, Reg6_q, Reg7_q, Reg8_q, Reg9_q, RegA_q, RegB_q,
       RegC_q, RegD_q, RegE_q, RegF_q;

  Pull_Resistor pull_resistor_1 (.node(Clock));
  Pull_Resistor pull_resistor_2 (.node(MasterReset));
  Register #(.width(16)) Reg0 (.D(InData), .en(demultiplexer_1_out0), .Q(Reg0_q), .clk(Clock), .clr(MasterReset));
  Register #(.width(16)) Reg1 (.D(InData), .en(demultiplexer_1_out1), .Q(Reg1_q), .clk(Clock), .clr(MasterReset));
  Multiplexer #(.select(4), .width(16)) multiplexer_1 (
    .in0(Reg0_q), .in1(Reg1_q), .in2(Reg2_q), .in3(Reg3_q), .in4(Reg4_q), .in5(Reg5_q), .in6(Reg6_q),
    .in7(Reg7_q), .in8(Reg8_q), .in9(Reg9_q), .in10(RegA_q), .in11(RegB_q), .in12(RegC_q), .in13(RegD_q),
    .in14(RegE_q), .in15(RegF_q), .out(AOutput), .sel(ASelect));
  Register #(.width(16)) Reg2 (.D(InData), .en(demultiplexer_1_out2), .Q(Reg2_q), .clk(Clock), .clr(MasterReset));
  Register #(.width(16)) Reg3 (.D(InData), .en(demultiplexer_1_out3), .Q(Reg3_q), .clk(Clock), .clr(MasterReset));
  Register #(.width(16)) Reg4 (.D(InData), .en(demultiplexer_1_out4), .Q(Reg4_q), .clk(Clock), .clr(MasterReset));
  Multiplexer #(.select(4), .width(16)) multiplexer_2 (
    .in0(Reg0_q), .in1(Reg1_q), .in2(Reg2_q), .in3(Reg3_q), .in4(Reg4_q), .in5(Reg5_q), .in6(Reg6_q),
    .in7(Reg7_q), .in8(Reg8_q), .in9(Reg9_q), .in10(RegA_q), .in11(RegB_q), .in12(RegC_q), .in13(RegD_q),
    .in14(RegE_q), .in15(RegF_q), .out(BOutput), .sel(BSelect));
  Register #(.width(16)) Reg5 (.D(InData), .en(demultiplexer_1_out5), .Q(Reg5_q), .clk(Clock), .clr(MasterReset));
  Register #(.width(16)) Reg6 (.D(InData), .en(demultiplexer_1_out6), .Q(Reg6_q), .clk(Clock), .clr(MasterReset));
  Demultiplexer #(.select(4)) demultiplexer_1 (
    .out0(demultiplexer_1_out0), .out1(demultiplexer_1_out1), .out2(demultiplexer_1_out2),
    .out3(demultiplexer_1_out3), .out4(demultiplexer_1_out4), .out5(demultiplexer_1_out5),
    .out6(demultiplexer_1_out6), .out7(demultiplexer_1_out7), .out8(demultiplexer_1_out8),
    .out9(demultiplexer_1_out9), .out10(demultiplexer_1_out10), .out11(demultiplexer_1_out11),
    .out12(demultiplexer_1_out12), .out13(demultiplexer_1_out13), .out14(demultiplexer_1_out14),
    .out15(demultiplexer_1_out15), .in(Write), .sel(Select));
  Register #(.width(16)) Reg7 (.D(InData), .en(demultiplexer_1_out7), .Q(Reg7_q), .clk(Clock), .clr(MasterReset));
  Register #(.width(16)) Reg8 (.D(InData), .en(demultiplexer_1_out8), .Q(Reg8_q), .clk(Clock), .clr(MasterReset));
  Register #(.width(16)) Reg9 (.D(InData), .en(demultiplexer_1_out9), .Q(Reg9_q), .clk(Clock), .clr(MasterReset));
  Register #(.width(16)) RegA (.D(InData), .en(demultiplexer_1_out10), .Q(RegA_q), .clk(Clock), .clr(MasterReset));
  Register #(.width(16)) RegC (.D(InData), .en(demultiplexer_1_out12), .Q(RegC_q), .clk(Clock), .clr(MasterReset));
  Register #(.width(16)) RegB (.D(InData), .en(demultiplexer_1_out11), .Q(RegB_q), .clk(Clock), .clr(MasterReset));
  Register #(.width(16)) RegD (.D(InData), .en(demultiplexer_1_out13), .Q(RegD_q), .clk(Clock), .clr(MasterReset));
  Register #(.width(16)) RegE (.D(InData), .en(demultiplexer_1_out14), .Q(RegE_q), .clk(Clock), .clr(MasterReset));
  Register #(.width(16)) RegF (.D(InData), .en(demultiplexer_1_out15), .Q(RegF_q), .clk(Clock), .clr(MasterReset));

  // Notes on the sheet:
  //   Clock: pull=down
  //   MasterReset: pull=down
endmodule
